// Logisim project f_project.circ as structural Verilog
module Decoder_2_4 (
  input  en,
  input  A,
  input  B,
  output Y0,
  output Y1,
  output Y2,
  output Y3
);

  wire not_1_out, not_2_out;

  not not_1 (not_1_out, A);
  not not_2 (not_2_out, B);
  and and_1 (Y0, not_1_out, en, not_2_out);
  and and_2 (Y1, not_1_out, en, B);
  and and_3 (Y2, A, en, not_2_out);
  and and_4 (Y3, A, en, B);
endmodule

module Decoder_3_8 (
  input  A,
  input  B,
  input  C,
  input  en,
  output Y0,
  output Y1,
  output Y2,
  output Y3,
  output Y4,
  output Y5,
  output Y6,
  output Y7
);

  wire and_1_out, and_2_out, not_1_out;

  not not_1 (not_1_out, A);
  and and_1 (and_1_out, not_1_out, en);
  and and_2 (and_2_out, A, en);
  Decoder_2_4 decoder_2_4_1 (.en(and_1_out), .A(B), .B(C), .Y0(Y0), .Y1(Y1), .Y2(Y2), .Y3(Y3));
  Decoder_2_4 decoder_2_4_2 (.en(and_2_out), .A(B), .B(C), .Y0(Y4), .Y1(Y5), .Y2(Y6), .Y3(Y7));
endmodule

module Decoder_4_16 (
  input  A,
  input  B,
  input  C,
  input  D,
  input  en,
  output Y0,
  output Y1,
  output Y2,
  output Y3,
  output Y4,
  output Y5,
  output Y6,
  output Y7,
  output Y8,
  output Y9,
  output Y10,
  output Y11,
  output Y12,
  output Y13,
  output Y14,
  output Y15
);

  wire and_1_out, and_2_out, not_1_out;

  not not_1 (not_1_out, A);
  and and_1 (and_1_out, not_1_out, en);
  and and_2 (and_2_out, A, en);
  Decoder_3_8 decoder_3_8_1 (
    .A(B), .B(C), .C(D), .en(and_1_out), .Y0(Y0), .Y1(Y1), .Y2(Y2), .Y3(Y3), .Y4(Y4), .Y5(Y5), .Y6(Y6),
    .Y7(Y7));
  Decoder_3_8 decoder_3_8_2 (
    .A(B), .B(C), .C(D), .en(and_2_out), .Y0(Y8), .Y1(Y9), .Y2(Y10), .Y3(Y11), .Y4(Y12), .Y5(Y13), .Y6(Y14),
    .Y7(Y15));
endmodule

module Decoder_4_16_new (
  input  [3:0] A,
  input  en,
  output Y0,
  output Y1,
  output Y2,
  output Y3,
  output Y4,
  output Y5,
  output Y6,
  output Y7,
  output Y8,
  output Y9,
  output Y10,
  output Y11,
  output Y12,
  output Y13,
  output Y14,
  output Y15
);

  Decoder_4_16 decoder_4_16_1 (
    .A(A[3]), .B(A[2]), .C(A[1]), .D(A[0]), .en(en), .Y0(Y0), .Y1(Y1), .Y2(Y2), .Y3(Y3), .Y4(Y4), .Y5(Y5),
    .Y6(Y6), .Y7(Y7), .Y8(Y8), .Y9(Y9), .Y10(Y10), .Y11(Y11), .Y12(Y12), .Y13(Y13), .Y14(Y14), .Y15(Y15));
endmodule

module Decoder_5_32 (
  input  [4:0] A,
  input  en,
  output [31:0] Y
);

  wire and_1_out, and_2_out, not_1_out;

  not not_1 (not_1_out, A[4]);
  and and_1 (and_1_out, not_1_out, en);
  and and_2 (and_2_out, A[4], en);
  Decoder_4_16_new decoder_4_16_new_1 (
    .A(A[3:0]), .en(and_1_out), .Y0(Y[0]), .Y1(Y[1]), .Y2(Y[2]), .Y3(Y[3]), .Y4(Y[4]), .Y5(Y[5]), .Y6(Y[6]),
    .Y7(Y[7]), .Y8(Y[8]), .Y9(Y[9]), .Y10(Y[10]), .Y11(Y[11]), .Y12(Y[12]), .Y13(Y[13]), .Y14(Y[14]),
    .Y15(Y[15]));
  Decoder_4_16_new decoder_4_16_new_2 (
    .A(A[3:0]), .en(and_2_out), .Y0(Y[16]), .Y1(Y[17]), .Y2(Y[18]), .Y3(Y[19]), .Y4(Y[20]), .Y5(Y[21]),
    .Y6(Y[22]), .Y7(Y[23]), .Y8(Y[24]), .Y9(Y[25]), .Y10(Y[26]), .Y11(Y[27]), .Y12(Y[28]), .Y13(Y[29]),
    .Y14(Y[30]), .Y15(Y[31]));

  // Other names for the same wires on the sheet: A_0_3[3:0] = A[3:0]; A_4 = A[4]

  // Notes on the sheet:
  //   A: initial=0xa
endmodule

module Decoder_SEG (
  input  DP_1,
  input  DP_0,
  input  S0,
  input  A3,
  input  A2,
  input  A1,
  input  A0,
  input  en,
  output DP1,
  output DP0,
  output a_1,
  output b_1,
  output c_1,
  output d_1,
  output e_1,
  output f_1,
  output g_1,
  output a_0,
  output b_0,
  output c_0,
  output d_0,
  output e_0,
  output f_0,
  output g_0
);

  wire a_0_d, a_0_h, a_d_e_f_1_d, a_f_1_h, b_0_d, b_0_h, c_0_d, c_0_h, d_0_d, d_0_h, e_0_d, e_0_h, f_0_d,
       f_0_h, g_0_d, g_0_h, g_1_d, g_1_h, Y0, Y1, Y2, Y3, Y4, Y5, Y6, Y7, Y8, Y9, Y10, Y11, Y12, Y13, Y14,
       Y15;

  Decoder_4_16 decoder_4_16_1 (
    .A(A3), .B(A2), .C(A1), .D(A0), .en(en), .Y0(Y0), .Y1(Y1), .Y2(Y2), .Y3(Y3), .Y4(Y4), .Y5(Y5), .Y6(Y6),
    .Y7(Y7), .Y8(Y8), .Y9(Y9), .Y10(Y10), .Y11(Y11), .Y12(Y12), .Y13(Y13), .Y14(Y14), .Y15(Y15));
  or or_1 (a_f_1_h, Y7, Y0, Y1, Y2, Y3, Y4, Y5, Y6, Y8, Y9, Y10, Y11, Y12, Y13, Y15, Y14);
  or or_2 (a_d_e_f_1_d, Y0, Y1, Y2, Y3, Y4, Y5, Y6, Y7, Y8, Y9);
  or or_3 (b_0_h, Y0, Y1, Y2, Y3, Y4, Y7, Y8, Y9, Y13, Y10);
  or or_4 (c_0_h, Y0, Y1, Y3, Y4, Y11, Y5, Y6, Y7, Y8, Y9, Y10, Y13);
  or or_5 (c_0_d, Y15, Y0, Y1, Y3, Y4, Y11, Y5, Y6, Y7, Y8, Y9, Y10, Y13, Y14);
  or or_6 (d_0_h, Y0, Y2, Y3, Y5, Y6, Y12, Y8, Y9, Y13, Y11, Y14);
  or or_7 (d_0_d, Y12, Y0, Y2, Y3, Y5, Y6, Y8, Y9, Y13, Y12, Y15, Y10);
  or or_8 (e_0_h, Y0, Y2, Y6, Y8, Y10, Y11, Y12, Y13, Y14, Y15);
  or or_9 (e_0_d, Y0, Y2, Y6, Y8, Y10, Y12);
  and and_1 (g_1_h, ~a_f_1_h, en);  // AND_Gate
  and and_2 (g_1_d, ~a_f_1_h, en);  // AND_Gate
  or or_10 (a_0_h, Y0, Y2, Y3, Y5, Y6, Y7, Y8, Y9, Y12, Y10, Y14, Y15);
  or or_11 (a_0_d, Y0, Y2, Y3, Y5, Y6, Y7, Y8, Y9, Y10, Y12, Y13, Y15);
  or or_12 (b_0_d, Y11, Y0, Y1, Y2, Y3, Y4, Y12, Y7, Y8, Y9, Y13, Y10, Y14);
  Selector_7_2_1 selector_7_2_1_1 (
    .S0(S0), .A16(a_f_1_h), .A15(a_f_1_h), .A14(a_f_1_h), .A13(a_f_1_h), .A12(a_f_1_h), .A11(a_f_1_h),
    .A10(g_1_h), .A06(a_d_e_f_1_d), .A05(a_f_1_h), .A04(a_f_1_h), .A03(a_d_e_f_1_d), .A02(a_d_e_f_1_d),
    .A01(a_d_e_f_1_d), .A00(g_1_d), .Y16(a_1), .Y15(b_1), .Y14(c_1), .Y13(d_1), .Y12(e_1), .Y11(f_1),
    .Y10(g_1));
  or or_13 (f_0_h, Y0, Y4, Y5, Y6, Y8, Y11, Y9, Y10, Y12, Y14, Y15);
  or or_14 (f_0_d, Y4, Y5, Y6, Y8, Y0, Y9, Y10, Y15, Y14);
  or or_15 (g_0_h, Y2, Y3, Y4, Y5, Y9, Y6, Y10, Y13, Y8, Y11, Y14, Y15);
  or or_16 (g_0_d, Y3, Y4, Y5, Y9, Y6, Y2, Y13, Y15, Y8, Y12, Y14);
  Selector_7_2_1 selector_7_2_1_2 (
    .S0(S0), .A16(a_0_h), .A15(b_0_h), .A14(c_0_h), .A13(d_0_h), .A12(e_0_h), .A11(f_0_h), .A10(g_0_h),
    .A06(a_0_d), .A05(b_0_d), .A04(c_0_d), .A03(d_0_d), .A02(e_0_d), .A01(f_0_d), .A00(g_0_d), .Y16(a_0),
    .Y15(b_0), .Y14(c_0), .Y13(d_0), .Y12(e_0), .Y11(f_0), .Y10(g_0));

  assign DP0 = DP_0;
  assign DP1 = DP_1;

  // Other names for the same wires on the sheet: b_c_1_d = a_f_1_h
endmodule

module Decoder_SEG_new (
  input  DP_1,
  input  DP_0,
  input  S0,
  input  [3:0] A,
  input  en,
  output DP1,
  output DP0,
  output a_1,
  output b_1,
  output c_1,
  output d_1,
  output e_1,
  output f_1,
  output g_1,
  output a_0,
  output b_0,
  output c_0,
  output d_0,
  output e_0,
  output f_0,
  output g_0
);

  Decoder_SEG decoder_seg_1 (
    .DP_1(DP_1), .DP_0(DP_0), .S0(S0), .A3(A[0]), .A2(A[1]), .A1(A[2]), .A0(A[3]), .en(en), .DP1(DP1),
    .DP0(DP0), .a_1(a_1), .b_1(b_1), .c_1(c_1), .d_1(d_1), .e_1(e_1), .f_1(f_1), .g_1(g_1), .a_0(a_0),
    .b_0(b_0), .c_0(c_0), .d_0(d_0), .e_0(e_0), .f_0(f_0), .g_0(g_0));
endmodule

module Decoder_min_seconds_SEG (
  input  [15:0] min_seconds,
  input  EN,
  output [13:0] a0_g0_a1_g1
);

  wire betw_10_20, betw_20_30, betw_30_40, betw_40_50, betw_50_60, comparator_16_1_g, comparator_16_2_g,
       comparator_16_2_l, comparator_16_3_g, comparator_16_3_l, comparator_16_4_g, comparator_16_4_l,
       comparator_16_5_g, comparator_16_5_l, comparator_16_6_l, E_10, E_20, E_30, E_40, E_50, E_60, L_10;
  wire [3:0] Ten, Units_digit;
  wire [15:0] Difference, selector_16_2_1_1_y, selector_16_2_1_2_y, selector_16_2_1_3_y, selector_16_2_1_4_y,
       selector_16_2_1_5_y, selector_16_2_1_6_y, selector_16_2_1_7_y, selector_16_2_1_8_y,
       selector_16_2_1_9_y, selector_16_2_1_10_y, selector_16_2_1_11_y, selector_16_2_1_12_y,
       selector_16_2_1_13_y, selector_16_2_1_14_y, selector_16_2_1_15_y, selector_16_2_1_16_y,
       selector_16_2_1_17_y, selector_16_2_1_18_y, selector_16_2_1_19_y, selector_16_2_1_20_y;
  wire [15:4] complement_adder_16_1_sum, selector_16_2_1_22_y;

  Selector_16_2_1 selector_16_2_1_1 (.S0(E_60), .A0({16{1'b0}}), .A1(16'h3c), .Y(selector_16_2_1_1_y));
  Selector_16_2_1 selector_16_2_1_2 (.S0(E_60), .A0({16{1'b0}}), .A1({16{1'b0}}), .Y(selector_16_2_1_2_y));
  Comparator_16 comparator_16_1 (
    .a(min_seconds), .b(16'ha), .G_IN(1'b0), .E_IN(1'b1), .L_IN(1'b0), .G(comparator_16_1_g), .E(E_10),
    .L(L_10));
  Comparator_16 comparator_16_2 (
    .a(min_seconds), .b(16'h14), .G_IN(1'b0), .E_IN(1'b1), .L_IN(1'b0), .G(comparator_16_2_g), .E(E_20),
    .L(comparator_16_2_l));
  Comparator_16 comparator_16_3 (
    .a(min_seconds), .b(16'h1e), .G_IN(1'b0), .E_IN(1'b1), .L_IN(1'b0), .G(comparator_16_3_g), .E(E_30),
    .L(comparator_16_3_l));
  Comparator_16 comparator_16_4 (
    .a(min_seconds), .b(16'h28), .G_IN(1'b0), .E_IN(1'b1), .L_IN(1'b0), .G(comparator_16_4_g), .E(E_40),
    .L(comparator_16_4_l));
  Comparator_16 comparator_16_5 (
    .a(min_seconds), .b(16'h32), .G_IN(1'b0), .E_IN(1'b1), .L_IN(1'b0), .G(comparator_16_5_g), .E(E_50),
    .L(comparator_16_5_l));
  Comparator_16 comparator_16_6 (
    .a(min_seconds), .b(16'h3c), .G_IN(1'b0), .E_IN(1'b1), .L_IN(1'b0), .E(E_60), .L(comparator_16_6_l));  // open: G
  Selector_16_2_1 selector_16_2_1_3 (.S0(betw_50_60), .A0(selector_16_2_1_1_y), .A1(16'h32), .Y(selector_16_2_1_3_y));
  Selector_16_2_1 selector_16_2_1_4 (.S0(betw_50_60), .A0(selector_16_2_1_2_y), .A1(16'h5), .Y(selector_16_2_1_4_y));
  and and_1 (betw_10_20, comparator_16_1_g, comparator_16_2_l);
  and and_2 (betw_20_30, comparator_16_2_g, comparator_16_3_l);
  and and_3 (betw_30_40, comparator_16_3_g, comparator_16_4_l);
  and and_4 (betw_40_50, comparator_16_4_g, comparator_16_5_l);
  and and_5 (betw_50_60, comparator_16_5_g, comparator_16_6_l);
  Selector_16_2_1 selector_16_2_1_5 (.S0(betw_40_50), .A0(selector_16_2_1_3_y), .A1(16'h28), .Y(selector_16_2_1_5_y));
  Selector_16_2_1 selector_16_2_1_6 (.S0(betw_40_50), .A0(selector_16_2_1_4_y), .A1(16'h4), .Y(selector_16_2_1_6_y));
  Selector_16_2_1 selector_16_2_1_7 (.S0(betw_30_40), .A0(selector_16_2_1_5_y), .A1(16'h1e), .Y(selector_16_2_1_7_y));
  // Probe on Difference
  Selector_16_2_1 selector_16_2_1_8 (.S0(betw_30_40), .A0(selector_16_2_1_6_y), .A1(16'h3), .Y(selector_16_2_1_8_y));
  Selector_16_2_1 selector_16_2_1_9 (.S0(betw_20_30), .A0(selector_16_2_1_7_y), .A1(16'h14), .Y(selector_16_2_1_9_y));
  Selector_16_2_1 selector_16_2_1_10 (.S0(betw_20_30), .A0(selector_16_2_1_8_y), .A1(16'h2), .Y(selector_16_2_1_10_y));
  Complement_Adder_16 complement_adder_16_1 (
    .symbol_a(1'b0), .a(min_seconds), .symbol_b(1'b1), .b(Difference),
    .sum({complement_adder_16_1_sum, Units_digit}));  // open: symbol_sum, Overflow
  // Probe on {complement_adder_16_1_sum, Units_digit}
  Selector_16_2_1 selector_16_2_1_11 (.S0(betw_10_20), .A0(selector_16_2_1_9_y), .A1(16'ha), .Y(selector_16_2_1_11_y));
  Selector_16_2_1 selector_16_2_1_12 (.S0(betw_10_20), .A0(selector_16_2_1_10_y), .A1(16'h1), .Y(selector_16_2_1_12_y));
  Decoder_SEG decoder_seg_1 (
    .S0(EN), .A3(Units_digit[3]), .A2(Units_digit[2]), .A1(Units_digit[1]), .A0(Units_digit[0]), .en(EN),
    .a_0(a0_g0_a1_g1[0]), .b_0(a0_g0_a1_g1[1]), .c_0(a0_g0_a1_g1[2]), .d_0(a0_g0_a1_g1[3]),
    .e_0(a0_g0_a1_g1[4]), .f_0(a0_g0_a1_g1[5]), .g_0(a0_g0_a1_g1[6]));  // open: DP_1, DP_0, DP1, DP0, a_1, b_1, c_1, d_1, e_1, f_1, g_1
  Decoder_SEG decoder_seg_2 (
    .S0(EN), .A3(Ten[3]), .A2(Ten[2]), .A1(Ten[1]), .A0(Ten[0]), .en(EN), .a_0(a0_g0_a1_g1[7]),
    .b_0(a0_g0_a1_g1[8]), .c_0(a0_g0_a1_g1[9]), .d_0(a0_g0_a1_g1[10]), .e_0(a0_g0_a1_g1[11]),
    .f_0(a0_g0_a1_g1[12]), .g_0(a0_g0_a1_g1[13]));  // open: DP_1, DP_0, DP1, DP0, a_1, b_1, c_1, d_1, e_1, f_1, g_1
  Selector_16_2_1 selector_16_2_1_13 (.S0(E_50), .A0(selector_16_2_1_11_y), .A1(16'h32), .Y(selector_16_2_1_13_y));
  Selector_16_2_1 selector_16_2_1_14 (.S0(E_50), .A0(selector_16_2_1_12_y), .A1(16'h5), .Y(selector_16_2_1_14_y));
  Selector_16_2_1 selector_16_2_1_15 (.S0(E_40), .A0(selector_16_2_1_13_y), .A1(16'h28), .Y(selector_16_2_1_15_y));
  Selector_16_2_1 selector_16_2_1_16 (.S0(E_40), .A0(selector_16_2_1_14_y), .A1(16'h4), .Y(selector_16_2_1_16_y));
  Selector_16_2_1 selector_16_2_1_17 (.S0(E_30), .A0(selector_16_2_1_15_y), .A1(16'h1e), .Y(selector_16_2_1_17_y));
  Selector_16_2_1 selector_16_2_1_18 (.S0(E_30), .A0(selector_16_2_1_16_y), .A1(16'h3), .Y(selector_16_2_1_18_y));
  Selector_16_2_1 selector_16_2_1_19 (.S0(E_20), .A0(selector_16_2_1_17_y), .A1(16'h14), .Y(selector_16_2_1_19_y));
  Selector_16_2_1 selector_16_2_1_20 (.S0(E_20), .A0(selector_16_2_1_18_y), .A1(16'h2), .Y(selector_16_2_1_20_y));
  Selector_16_2_1 selector_16_2_1_21 (.S0(E_10), .A0(selector_16_2_1_19_y), .A1(16'ha), .Y(Difference));
  Selector_16_2_1 selector_16_2_1_22 (
    .S0(E_10), .A0(selector_16_2_1_20_y), .A1(16'h1), .Y({selector_16_2_1_22_y, Ten}));

  // Other names for the same wires on the sheet: a_0 = a0_g0_a1_g1[0]; b_0 = a0_g0_a1_g1[1]; c_0 = a0_g0_a1_g1[2];
  //   d_0 = a0_g0_a1_g1[3]; e_0 = a0_g0_a1_g1[4]; f_0 = a0_g0_a1_g1[5]; g_0 = a0_g0_a1_g1[6]; a_1 = a0_g0_a1_g1[7];
  //   b_1 = a0_g0_a1_g1[8]; c_1 = a0_g0_a1_g1[9]; d_1 = a0_g0_a1_g1[10]; e_1 = a0_g0_a1_g1[11]; f_1 = a0_g0_a1_g1[12];
  //   g_1 = a0_g0_a1_g1[13]; seconds[15:0] = min_seconds
endmodule

module Decoder_SEG_Temple (
  input  DP_1,
  input  DP_0,
  input  S0,
  input  A3,
  input  A2,
  input  A1,
  input  A0,
  input  en
);

  wire a_0, a_1, b_0, b_1, c_0, c_1, d_0, d_1, DP0, DP1, e_0, e_1, f_0, f_1, g_0, g_1;

  Decoder_SEG decoder_seg_1 (
    .DP_1(DP_1), .DP_0(DP_0), .S0(S0), .A3(A3), .A2(A2), .A1(A1), .A0(A0), .en(en), .DP1(DP1), .DP0(DP0),
    .a_1(a_1), .b_1(b_1), .c_1(c_1), .d_1(d_1), .e_1(e_1), .f_1(f_1), .g_1(g_1), .a_0(a_0), .b_0(b_0),
    .c_0(c_0), .d_0(d_0), .e_0(e_0), .f_0(f_0), .g_0(g_0));
  _7_Segment_Display u_7_segment_display_1 (.g(g_1), .f(f_1), .a(a_1), .b(b_1), .e(e_1), .d(d_1), .c(c_1));  // open: dp
  _7_Segment_Display u_7_segment_display_2 (.g(g_0), .f(f_0), .a(a_0), .b(b_0), .e(e_0), .d(d_0), .c(c_0));  // open: dp
endmodule

module Encoder_16_4 (
  input  A15,
  input  A14,
  input  A13,
  input  A12,
  input  A11,
  input  A10,
  input  A9,
  input  A8,
  input  A7,
  input  A6,
  input  A5,
  input  A4,
  input  A3,
  input  A2,
  input  A1,
  input  A0,
  input  en,
  output Y3,
  output Y2,
  output Y1,
  output Y0
);

  wire o_0, o_1, o_2, o_3, o_4, o_5, O_6, o_7, or_9_out;

  or or_1 (o_7, A15, A7);
  or or_2 (O_6, A6, A14);
  or or_3 (o_5, A5, A13);
  or or_4 (o_4, A4, A12);
  or or_5 (o_3, A3, A11);
  or or_6 (o_2, A2, A10);
  or or_7 (o_1, A1, A9);
  or or_8 (o_0, A0, A8);
  or or_9 (or_9_out, A15, A14, A13, A12, A11, A10, A9, A8);
  and and_1 (Y3, en, or_9_out);
  Encoder_8_3 encoder_8_3_1 (
    .A7(o_7), .A6(O_6), .A5(o_5), .A4(o_4), .A3(o_3), .A2(o_2), .A1(o_1), .A0(o_0), .en(en), .Y2(Y2),
    .Y1(Y1), .Y0(Y0));
endmodule

module Encoder_4_2 (
  input  A3,
  input  A2,
  input  A1,
  input  A0,
  input  en,
  output Y1,
  output Y0
);

  wire or_1_out, or_2_out;

  or or_1 (or_1_out, A3, A2);
  or or_2 (or_2_out, A1, A3);
  and and_1 (Y1, en, or_1_out);
  and and_2 (Y0, or_2_out, en);
endmodule

module Encoder_8_3 (
  input  A7,
  input  A6,
  input  A5,
  input  A4,
  input  A3,
  input  A2,
  input  A1,
  input  A0,
  input  en,
  output Y2,
  output Y1,
  output Y0
);

  wire o_0, o_1, o_2, o_3, or_5_out;

  or or_1 (o_3, A7, A3);
  or or_2 (o_2, A6, A2);
  or or_3 (o_1, A5, A1);
  or or_4 (o_0, A4, A0);
  or or_5 (or_5_out, A7, A6, A5, A4);
  Encoder_4_2 encoder_4_2_1 (.A3(o_3), .A2(o_2), .A1(o_1), .A0(o_0), .en(en), .Y1(Y1), .Y0(Y0));
  and and_1 (Y2, en, or_5_out);
endmodule

module Priority_Encoder_4_2 (
  input  A3,
  input  A2,
  input  A1,
  input  A0,
  input  en,
  output Y1,
  output Y0,
  output ef
);

  wire and_1_out, and_2_out, or_1_out, or_2_out, or_3_out;

  buf and_1 (and_1_out, A2);  // AND_Gate AND_Gate
  and and_2 (and_2_out, ~A3, ~A2, A1);  // AND_Gate
  and and_3 (Y1, en, or_1_out);
  or or_1 (or_1_out, A3, and_1_out);
  and and_4 (Y0, en, or_2_out);
  or or_2 (or_2_out, A3, and_2_out);
  or or_3 (or_3_out, A3, A2, A1, A0);
  and and_5 (ef, or_3_out, en);
endmodule

module Priority_Encoder_16_4 (
  input  A15,
  input  A14,
  input  A13,
  input  A12,
  input  A11,
  input  A10,
  input  A9,
  input  A8,
  input  A7,
  input  A6,
  input  A5,
  input  A4,
  input  A3,
  input  A2,
  input  A1,
  input  A0,
  input  en,
  output Y3,
  output Y2,
  output Y1,
  output Y0,
  output ef
);

  wire and_1_out, and_2_out, and_3_out, and_4_out, and_5_out, and_6_out, ef0, or_1_out, Y00, Y01, Y02, Y10,
       Y11, Y12;

  Priority_Encoder_8_3 priority_encoder_8_3_1 (
    .A7(A15), .A6(A14), .A5(A13), .A4(A12), .A3(A11), .A2(A10), .A1(A9), .A0(A8), .en(en), .Y2(Y12),
    .Y1(Y11), .Y0(Y10), .ef(Y3));
  Priority_Encoder_8_3 priority_encoder_8_3_2 (
    .A7(A7), .A6(A6), .A5(A5), .A4(A4), .A3(A3), .A2(A2), .A1(A1), .A0(A0), .en(en), .Y2(Y02), .Y1(Y01),
    .Y0(Y00), .ef(ef0));
  and and_1 (and_1_out, Y12, Y3);
  and and_2 (and_2_out, Y02, ~Y3);  // AND_Gate
  and and_3 (and_3_out, Y11, Y3);
  and and_4 (and_4_out, Y01, ~Y3);  // AND_Gate
  and and_5 (and_5_out, Y10, Y3);
  and and_6 (and_6_out, Y00, ~Y3);  // AND_Gate
  or or_1 (or_1_out, A15, A14, A13, A12, A11, A10, A9, A8, A7, A6, A2, A5, A4, A3, A1, A0);
  and and_7 (ef, or_1_out, en);
  or or_2 (Y2, and_1_out, and_2_out);
  or or_3 (Y1, and_3_out, and_4_out);
  or or_4 (Y0, and_5_out, and_6_out);

  // Other names for the same wires on the sheet: ef1 = Y3
endmodule

module Priority_Encoder_8_3 (
  input  A7,
  input  A6,
  input  A5,
  input  A4,
  input  A3,
  input  A2,
  input  A1,
  input  A0,
  input  en,
  output Y2,
  output Y1,
  output Y0,
  output ef
);

  wire and_1_out, and_2_out, and_3_out, and_4_out, ef0, or_1_out, Y00, Y01, Y10, Y11;

  Priority_Encoder_4_2 priority_encoder_4_2_1 (
    .A3(A3), .A2(A2), .A1(A1), .A0(A0), .en(en), .Y1(Y01), .Y0(Y00), .ef(ef0));
  Priority_Encoder_4_2 priority_encoder_4_2_2 (
    .A3(A7), .A2(A6), .A1(A5), .A0(A4), .en(en), .Y1(Y11), .Y0(Y10), .ef(Y2));
  and and_1 (and_1_out, Y11, Y2);
  and and_2 (and_2_out, Y01, ~Y2);  // AND_Gate
  and and_3 (and_3_out, Y10, Y2);
  and and_4 (and_4_out, Y00, ~Y2);  // AND_Gate
  or or_1 (or_1_out, A7, A4, A6, A5, A3, A2, A1, A0);
  or or_2 (Y1, and_1_out, and_2_out);
  or or_3 (Y0, and_3_out, and_4_out);
  and and_5 (ef, or_1_out, en);

  // Other names for the same wires on the sheet: ef1 = Y2
endmodule

module Selector_1_2_1 (
  input  S,
  input  A1,
  input  A0,
  output Y
);

  wire and_1_out, and_2_out;

  and and_1 (and_1_out, S, A1);
  and and_2 (and_2_out, ~S, A0);  // AND_Gate
  or or_1 (Y, and_1_out, and_2_out);
endmodule

module Selector_2_2_1 (
  input  S0,
  input  [1:0] A1,
  input  [1:0] A0,
  output [1:0] Y
);

  Selector_1_2_1 selector_1_2_1_1 (.S(S0), .A1(A1[1]), .A0(A0[1]), .Y(Y[1]));
  Selector_1_2_1 selector_1_2_1_2 (.S(S0), .A1(A1[0]), .A0(A0[0]), .Y(Y[0]));
endmodule

module Selector_4_2_1 (
  input  S0,
  input  [3:0] A1,
  input  [3:0] A0,
  output [3:0] Y
);

  Selector_1_2_1 selector_1_2_1_1 (.S(S0), .A1(A1[3]), .A0(A0[3]), .Y(Y[3]));
  Selector_1_2_1 selector_1_2_1_2 (.S(S0), .A1(A1[2]), .A0(A0[2]), .Y(Y[2]));
  Selector_1_2_1 selector_1_2_1_3 (.S(S0), .A1(A1[1]), .A0(A0[1]), .Y(Y[1]));
  Selector_1_2_1 selector_1_2_1_4 (.S(S0), .A1(A1[0]), .A0(A0[0]), .Y(Y[0]));
endmodule

module Selector_5_2_1 (
  input  S0,
  input  [4:0] A1,
  input  [4:0] A0,
  output [4:0] Y
);

  wire [7:5] selector_8_2_1_1_y;

  Selector_8_2_1 selector_8_2_1_1 (.S0(S0), .A1({3'b000, A1}), .A0({3'b000, A0}), .Y({selector_8_2_1_1_y, Y}));
endmodule

module Selector_8_2_1 (
  input  S0,
  input  [7:0] A1,
  input  [7:0] A0,
  output [7:0] Y
);

  Selector_4_2_1 selector_4_2_1_1 (.S0(S0), .A1(A1[3:0]), .A0(A0[3:0]), .Y(Y[3:0]));
  Selector_4_2_1 selector_4_2_1_2 (.S0(S0), .A1(A1[7:4]), .A0(A0[7:4]), .Y(Y[7:4]));

  // Other names for the same wires on the sheet: A00[3:0] = A0[3:0]; A01[3:0] = A0[7:4]; A10[3:0] = A1[3:0];
  //   A11[3:0] = A1[7:4]
endmodule

module Selector_8_4_1 (
  input  [1:0] S,
  input  [7:0] A3,
  input  [7:0] A2,
  input  [7:0] A1,
  input  [7:0] A0,
  output [7:0] Y
);

  wire [7:0] selector_8_2_1_1_y, selector_8_2_1_2_y;

  Selector_8_2_1 selector_8_2_1_1 (.S0(S[0]), .A1(A3), .A0(A2), .Y(selector_8_2_1_1_y));
  Selector_8_2_1 selector_8_2_1_2 (.S0(S[0]), .A1(A1), .A0(A0), .Y(selector_8_2_1_2_y));
  Selector_8_2_1 selector_8_2_1_3 (.S0(S[1]), .A1(selector_8_2_1_1_y), .A0(selector_8_2_1_2_y), .Y(Y));
endmodule

module Selector_8_16_1 (
  input  [3:0] S,
  input  [7:0] A15,
  input  [7:0] A14,
  input  [7:0] A13,
  input  [7:0] A12,
  input  [7:0] A11,
  input  [7:0] A10,
  input  [7:0] A9,
  input  [7:0] A8,
  input  [7:0] A7,
  input  [7:0] A6,
  input  [7:0] A5,
  input  [7:0] A4,
  input  [7:0] A3,
  input  [7:0] A2,
  input  [7:0] A1,
  input  [7:0] A0,
  output [7:0] Y
);

  wire [7:0] selector_8_4_1_1_y, selector_8_4_1_2_y, selector_8_4_1_3_y, selector_8_4_1_4_y;

  Selector_8_4_1 selector_8_4_1_1 (.S(S[1:0]), .A3(A15), .A2(A14), .A1(A13), .A0(A12), .Y(selector_8_4_1_1_y));
  Selector_8_4_1 selector_8_4_1_2 (.S(S[1:0]), .A3(A11), .A2(A10), .A1(A9), .A0(A8), .Y(selector_8_4_1_2_y));
  Selector_8_4_1 selector_8_4_1_3 (.S(S[1:0]), .A3(A7), .A2(A6), .A1(A5), .A0(A4), .Y(selector_8_4_1_3_y));
  Selector_8_4_1 selector_8_4_1_4 (.S(S[1:0]), .A3(A3), .A2(A2), .A1(A1), .A0(A0), .Y(selector_8_4_1_4_y));
  Selector_8_4_1 selector_8_4_1_5 (
    .S(S[3:2]), .A3(selector_8_4_1_1_y), .A2(selector_8_4_1_2_y), .A1(selector_8_4_1_3_y),
    .A0(selector_8_4_1_4_y), .Y(Y));

  // Other names for the same wires on the sheet: S0[1:0] = S[1:0]; S1[1:0] = S[3:2]
endmodule

module Selector_1_4_1 (
  input  S1,
  input  S0,
  input  A3,
  input  A2,
  input  A1,
  input  A0,
  output Y
);

  wire Y0, Y1;

  Selector_1_2_1 selector_1_2_1_1 (.S(S0), .A1(A3), .A0(A2), .Y(Y1));
  Selector_1_2_1 selector_1_2_1_2 (.S(S0), .A1(A1), .A0(A0), .Y(Y0));
  Selector_1_2_1 selector_1_2_1_3 (.S(S1), .A1(Y1), .A0(Y0), .Y(Y));
endmodule

module Selector_3_4_1 (
  input  S1,
  input  S0,
  input  A32,
  input  A31,
  input  A30,
  input  A22,
  input  A21,
  input  A20,
  input  A12,
  input  A11,
  input  A10,
  input  A02,
  input  A01,
  input  A00,
  output Y2,
  output Y1,
  output Y0
);

  Selector_1_4_1 selector_1_4_1_1 (.S1(S1), .S0(S0), .A3(A32), .A2(A22), .A1(A12), .A0(A02), .Y(Y2));
  Selector_1_4_1 selector_1_4_1_2 (.S1(S1), .S0(S0), .A3(A31), .A2(A21), .A1(A11), .A0(A01), .Y(Y1));
  Selector_1_4_1 selector_1_4_1_3 (.S1(S1), .S0(S0), .A3(A30), .A2(A20), .A1(A10), .A0(A00), .Y(Y0));
endmodule

module Selector_7_2_1 (
  input  S0,
  input  A16,
  input  A15,
  input  A14,
  input  A13,
  input  A12,
  input  A11,
  input  A10,
  input  A06,
  input  A05,
  input  A04,
  input  A03,
  input  A02,
  input  A01,
  input  A00,
  output Y16,
  output Y15,
  output Y14,
  output Y13,
  output Y12,
  output Y11,
  output Y10
);

  Selector_1_2_1 selector_1_2_1_1 (.S(S0), .A1(A16), .A0(A06), .Y(Y16));
  Selector_1_2_1 selector_1_2_1_2 (.S(S0), .A1(A15), .A0(A05), .Y(Y15));
  Selector_1_2_1 selector_1_2_1_3 (.S(S0), .A1(A14), .A0(A04), .Y(Y14));
  Selector_1_2_1 selector_1_2_1_4 (.S(S0), .A1(A13), .A0(A03), .Y(Y13));
  Selector_1_2_1 selector_1_2_1_5 (.S(S0), .A1(A12), .A0(A02), .Y(Y12));
  Selector_1_2_1 selector_1_2_1_6 (.S(S0), .A1(A11), .A0(A01), .Y(Y11));
  Selector_1_2_1 selector_1_2_1_7 (.S(S0), .A1(A10), .A0(A00), .Y(Y10));
endmodule

module Selector_16_2_1 (
  input  S0,
  input  [15:0] A0,
  input  [15:0] A1,
  output [15:0] Y
);

  Selector_8_2_1 selector_8_2_1_1 (.S0(S0), .A1(A1[7:0]), .A0(A0[7:0]), .Y(Y[7:0]));
  Selector_8_2_1 selector_8_2_1_2 (.S0(S0), .A1(A1[15:8]), .A0(A0[15:8]), .Y(Y[15:8]));
endmodule

module Selector_32_2_1 (
  input  S0,
  input  [31:0] A1,
  input  [31:0] A0,
  output [31:0] Y
);

  Selector_16_2_1 selector_16_2_1_1 (.S0(S0), .A0(A0[15:0]), .A1(A1[15:0]), .Y(Y[15:0]));
  Selector_16_2_1 selector_16_2_1_2 (.S0(S0), .A0(A0[31:16]), .A1(A1[31:16]), .Y(Y[31:16]));

  // Other names for the same wires on the sheet: A0_0_15[15:0] = A0[15:0]; A0_16_31[15:0] = A0[31:16];
  //   A1_0_15[15:0] = A1[15:0]; A1_16_31[15:0] = A1[31:16]
endmodule

module Selector_32_4_1 (
  input  [1:0] S,
  input  [31:0] A3,
  input  [31:0] A2,
  input  [31:0] A1,
  input  [31:0] A0,
  output [31:0] Y
);

  wire [31:0] selector_32_2_1_1_y, selector_32_2_1_2_y;

  Selector_32_2_1 selector_32_2_1_1 (.S0(S[0]), .A1(A3), .A0(A2), .Y(selector_32_2_1_1_y));
  Selector_32_2_1 selector_32_2_1_2 (.S0(S[0]), .A1(A1), .A0(A0), .Y(selector_32_2_1_2_y));
  Selector_32_2_1 selector_32_2_1_3 (.S0(S[1]), .A1(selector_32_2_1_1_y), .A0(selector_32_2_1_2_y), .Y(Y));
endmodule

module Selector_32_16_1 (
  input  [3:0] S,
  input  [31:0] A15,
  input  [31:0] A14,
  input  [31:0] A13,
  input  [31:0] A12,
  input  [31:0] A11,
  input  [31:0] A10,
  input  [31:0] A9,
  input  [31:0] A8,
  input  [31:0] A7,
  input  [31:0] A6,
  input  [31:0] A5,
  input  [31:0] A4,
  input  [31:0] A3,
  input  [31:0] A2,
  input  [31:0] A1,
  input  [31:0] A0,
  output [31:0] Y
);

  wire [31:0] selector_32_4_1_1_y, selector_32_4_1_2_y, selector_32_4_1_3_y, selector_32_4_1_4_y;

  Selector_32_4_1 selector_32_4_1_1 (.S(S[1:0]), .A3(A15), .A2(A14), .A1(A13), .A0(A12), .Y(selector_32_4_1_1_y));
  Selector_32_4_1 selector_32_4_1_2 (.S(S[1:0]), .A3(A11), .A2(A10), .A1(A9), .A0(A8), .Y(selector_32_4_1_2_y));
  Selector_32_4_1 selector_32_4_1_3 (.S(S[1:0]), .A3(A7), .A2(A6), .A1(A5), .A0(A4), .Y(selector_32_4_1_3_y));
  Selector_32_4_1 selector_32_4_1_4 (.S(S[1:0]), .A3(A3), .A2(A2), .A1(A1), .A0(A0), .Y(selector_32_4_1_4_y));
  Selector_32_4_1 selector_32_4_1_5 (
    .S(S[3:2]), .A3(selector_32_4_1_1_y), .A2(selector_32_4_1_2_y), .A1(selector_32_4_1_3_y),
    .A0(selector_32_4_1_4_y), .Y(Y));

  // Other names for the same wires on the sheet: S0[1:0] = S[1:0]; S1[1:0] = S[3:2]
endmodule

module Selector_32_32_1 (
  input  [4:0] S,
  input  [31:0] A31,
  input  [31:0] A30,
  input  [31:0] A29,
  input  [31:0] A28,
  input  [31:0] A27,
  input  [31:0] A26,
  input  [31:0] A25,
  input  [31:0] A24,
  input  [31:0] A23,
  input  [31:0] A22,
  input  [31:0] A21,
  input  [31:0] A20,
  input  [31:0] A19,
  input  [31:0] A18,
  input  [31:0] A17,
  input  [31:0] A16,
  input  [31:0] A15,
  input  [31:0] A14,
  input  [31:0] A13,
  input  [31:0] A12,
  input  [31:0] A11,
  input  [31:0] A10,
  input  [31:0] A9,
  input  [31:0] A8,
  input  [31:0] A7,
  input  [31:0] A6,
  input  [31:0] A5,
  input  [31:0] A4,
  input  [31:0] A3,
  input  [31:0] A2,
  input  [31:0] A1,
  input  [31:0] A0,
  output [31:0] Y
);

  wire [31:0] selector_32_16_1_1_y, selector_32_16_1_2_y;

  Selector_32_16_1 selector_32_16_1_1 (
    .S(S[3:0]), .A15(A31), .A14(A30), .A13(A29), .A12(A28), .A11(A27), .A10(A26), .A9(A25), .A8(A24),
    .A7(A23), .A6(A22), .A5(A21), .A4(A20), .A3(A19), .A2(A18), .A1(A17), .A0(A16), .Y(selector_32_16_1_1_y));
  Selector_32_16_1 selector_32_16_1_2 (
    .S(S[3:0]), .A15(A15), .A14(A14), .A13(A13), .A12(A12), .A11(A11), .A10(A10), .A9(A9), .A8(A8), .A7(A7),
    .A6(A6), .A5(A5), .A4(A4), .A3(A3), .A2(A2), .A1(A1), .A0(A0), .Y(selector_32_16_1_2_y));
  Selector_32_2_1 selector_32_2_1_1 (.S0(S[4]), .A1(selector_32_16_1_1_y), .A0(selector_32_16_1_2_y), .Y(Y));

  // Other names for the same wires on the sheet: S0[3:0] = S[3:0]; S1 = S[4]
endmodule

module Comparator_2 (
  input  [1:0] A,
  input  [1:0] B,
  input  G_IN,
  input  E_IN,
  input  L_IN,
  output G,
  output E,
  output L
);

  wire and_1_out, and_2_out, and_4_out, e0, e1, local_E, local_G, local_L, or_1_out, or_4_out, xor_1_out,
       xor_2_out;

  and and_1 (and_1_out, A[1], ~B[1]);  // AND_Gate
  and and_2 (and_2_out, e1, A[0], ~B[0]);  // AND_Gate
  xor xor_1 (xor_1_out, A[1], B[1]);
  not not_1 (e1, xor_1_out);
  xor xor_2 (xor_2_out, A[0], B[0]);
  not not_2 (e0, xor_2_out);
  or or_1 (or_1_out, local_G, local_E);
  not not_3 (local_L, or_1_out);
  or or_2 (local_G, and_1_out, and_2_out);
  and and_3 (local_E, e1, e0);
  and and_4 (and_4_out, E_IN, local_G);
  or or_3 (G, G_IN, and_4_out);
  and and_5 (E, local_E, E_IN);
  or or_4 (or_4_out, G, E);
  not not_4 (L, or_4_out);
endmodule

module Comparator_3 (
  input  [2:0] A,
  input  [2:0] B,
  input  G_IN,
  input  E_IN,
  input  L_IN,
  output G,
  output E,
  output L
);

  Comparator_4 comparator_4_1 (
    .A3(1'b0), .A2(A[2]), .A1(A[1]), .A0(A[0]), .B3(1'b0), .B2(B[2]), .B1(B[1]), .B0(B[0]), .G_IN(G_IN),
    .E_IN(E_IN), .L_IN(L_IN), .G(G), .E(E), .L(L));
endmodule

module Comparator_4 (
  input  A3,
  input  A2,
  input  A1,
  input  A0,
  input  B3,
  input  B2,
  input  B1,
  input  B0,
  input  G_IN,
  input  E_IN,
  input  L_IN,
  output G,
  output E,
  output L
);

  wire and_1_out, and_2_out, and_3_out, and_4_out, and_6_out, e0, e1, e2, e3, local_E, local_G, local_L,
       or_1_out, or_4_out, xor_1_out, xor_2_out, xor_3_out, xor_4_out;

  and and_1 (and_1_out, A3, ~B3);  // AND_Gate
  and and_2 (and_2_out, e3, A2, ~B2);  // AND_Gate
  and and_3 (and_3_out, e3, e2, A1, ~B1);  // AND_Gate
  and and_4 (and_4_out, e3, e2, e1, A0, ~B0);  // AND_Gate
  xor xor_1 (xor_1_out, A3, B3);
  not not_1 (e3, xor_1_out);
  xor xor_2 (xor_2_out, A2, B2);
  not not_2 (e2, xor_2_out);
  xor xor_3 (xor_3_out, A1, B1);
  not not_3 (e1, xor_3_out);
  xor xor_4 (xor_4_out, A0, B0);
  not not_4 (e0, xor_4_out);
  or or_1 (or_1_out, local_G, local_E);
  not not_5 (local_L, or_1_out);
  or or_2 (local_G, and_1_out, and_2_out, and_3_out, and_4_out);
  and and_5 (local_E, e3, e2, e1, e0);
  and and_6 (and_6_out, E_IN, local_G);
  or or_3 (G, G_IN, and_6_out);
  and and_7 (E, local_E, E_IN);
  or or_4 (or_4_out, G, E);
  not not_6 (L, or_4_out);
endmodule

module Comparator_7 (
  input  [6:0] A,
  input  [6:0] B,
  input  G_IN,
  input  E_IN,
  input  L_IN,
  output G,
  output E,
  output L
);

  Comparator_8 comparator_8_1 (
    .a({1'b0, A}), .b({1'b0, B}), .G_IN(G_IN), .E_IN(E_IN), .L_IN(L_IN), .G(G), .E(E), .L(L));
endmodule

module Comparator_8 (
  input  [7:0] a,
  input  [7:0] b,
  input  G_IN,
  input  E_IN,
  input  L_IN,
  output G,
  output E,
  output L
);

  wire comparator_4_2_e, comparator_4_2_g, comparator_4_2_l;

  Comparator_4 comparator_4_1 (
    .A3(a[3]), .A2(a[2]), .A1(a[1]), .A0(a[0]), .B3(b[3]), .B2(b[2]), .B1(b[1]), .B0(b[0]),
    .G_IN(comparator_4_2_g), .E_IN(comparator_4_2_e), .L_IN(comparator_4_2_l), .G(G), .E(E), .L(L));
  Comparator_4 comparator_4_2 (
    .A3(a[7]), .A2(a[6]), .A1(a[5]), .A0(a[4]), .B3(b[7]), .B2(b[6]), .B1(b[5]), .B0(b[4]), .G_IN(G_IN),
    .E_IN(E_IN), .L_IN(L_IN), .G(comparator_4_2_g), .E(comparator_4_2_e), .L(comparator_4_2_l));

  // Other names for the same wires on the sheet: a0[3:0] = a[3:0]; a1[3:0] = a[7:4]; b0[3:0] = b[3:0];
  //   b1[3:0] = b[7:4]
endmodule

module Comparator_16 (
  input  [15:0] a,
  input  [15:0] b,
  input  G_IN,
  input  E_IN,
  input  L_IN,
  output G,
  output E,
  output L
);

  wire comparator_4_2_e, comparator_4_2_g, comparator_4_2_l, comparator_4_3_e, comparator_4_3_g,
       comparator_4_3_l, comparator_4_4_e, comparator_4_4_g, comparator_4_4_l;
  wire [3:0] undriven;

  Comparator_4 comparator_4_1 (
    .A3(a[3]), .A2(a[2]), .A1(a[1]), .A0(a[0]), .B3(b[3]), .B2(b[2]), .B1(b[1]), .B0(b[0]),
    .G_IN(comparator_4_2_g), .E_IN(comparator_4_2_e), .L_IN(comparator_4_2_l), .G(G), .E(E), .L(L));
  Comparator_4 comparator_4_2 (
    .A3(a[7]), .A2(a[6]), .A1(a[5]), .A0(a[4]), .B3(b[7]), .B2(b[6]), .B1(b[5]), .B0(b[4]),
    .G_IN(comparator_4_3_g), .E_IN(comparator_4_3_e), .L_IN(comparator_4_3_l), .G(comparator_4_2_g),
    .E(comparator_4_2_e), .L(comparator_4_2_l));
  Comparator_4 comparator_4_3 (
    .A3(undriven[3]), .A2(undriven[2]), .A1(undriven[1]), .A0(undriven[0]), .B3(b[11]), .B2(b[10]),
    .B1(b[9]), .B0(b[8]), .G_IN(comparator_4_4_g), .E_IN(comparator_4_4_e), .L_IN(comparator_4_4_l),
    .G(comparator_4_3_g), .E(comparator_4_3_e), .L(comparator_4_3_l));
  Comparator_4 comparator_4_4 (
    .A3(a[15]), .A2(a[14]), .A1(a[13]), .A0(a[12]), .B3(b[15]), .B2(b[14]), .B1(b[13]), .B0(b[12]),
    .G_IN(G_IN), .E_IN(E_IN), .L_IN(L_IN), .G(comparator_4_4_g), .E(comparator_4_4_e), .L(comparator_4_4_l));

  // Other names for the same wires on the sheet: a0[3:0] = a[3:0]; a1[3:0] = a[7:4]; a2[3:0] = a[11:8];
  //   a3[3:0] = a[15:12]; b0[3:0] = b[3:0]; b1[3:0] = b[7:4]; b2[3:0] = b[11:8]; b3[3:0] = b[15:12]
endmodule

module Comparator_32 (
  input  [31:0] a,
  input  [31:0] b,
  input  G_IN,
  input  E_IN,
  input  L_IN,
  output G,
  output E,
  output L
);

  wire comparator_16_2_e, comparator_16_2_g, comparator_16_2_l;

  Comparator_16 comparator_16_1 (
    .a(a[15:0]), .b(b[15:0]), .G_IN(comparator_16_2_g), .E_IN(comparator_16_2_e), .L_IN(comparator_16_2_l),
    .G(G), .E(E), .L(L));
  Comparator_16 comparator_16_2 (
    .a(a[31:16]), .b(b[31:16]), .G_IN(G_IN), .E_IN(E_IN), .L_IN(L_IN), .G(comparator_16_2_g),
    .E(comparator_16_2_e), .L(comparator_16_2_l));

  // Other names for the same wires on the sheet: a0[15:0] = a[15:0]; a1[15:0] = a[31:16]; b0[15:0] = b[15:0];
  //   b1[15:0] = b[31:16]
endmodule

module Adder_full (
  input  cin,
  input  a,
  input  b,
  output sum,
  output cout
);

  wire adder_half_1_cout, adder_half_1_sum, adder_half_2_cout;

  Adder_half adder_half_1 (.a(a), .b(b), .sum(adder_half_1_sum), .cout(adder_half_1_cout));
  or or_1 (cout, adder_half_1_cout, adder_half_2_cout);
  Adder_half adder_half_2 (.a(cin), .b(adder_half_1_sum), .sum(sum), .cout(adder_half_2_cout));
endmodule

module Adder_half (
  input  a,
  input  b,
  output sum,
  output cout
);

  xor xor_1 (sum, a, b);
  and and_1 (cout, b, a);
endmodule

module Adder_full_4 (
  input  [3:0] A,
  input  [3:0] B,
  input  Cin,
  output Cout,
  output [3:0] S
);

  wire adder_full_2_cout, adder_full_3_cout, adder_full_4_cout;

  Adder_full adder_full_1 (.cin(adder_full_2_cout), .a(A[3]), .b(B[3]), .sum(S[3]), .cout(Cout));
  Adder_full adder_full_2 (.cin(adder_full_3_cout), .a(A[2]), .b(B[2]), .sum(S[2]), .cout(adder_full_2_cout));
  Adder_full adder_full_3 (.cin(adder_full_4_cout), .a(A[1]), .b(B[1]), .sum(S[1]), .cout(adder_full_3_cout));
  Adder_full adder_full_4 (.cin(Cin), .a(A[0]), .b(B[0]), .sum(S[0]), .cout(adder_full_4_cout));
endmodule

module Adder_full_8 (
  input  [7:0] A,
  input  [7:0] B,
  input  Cin,
  output Cout,
  output [7:0] S
);

  wire adder_full_4_2_cout;

  Adder_full_4 adder_full_4_1 (.A(A[7:4]), .B(B[7:4]), .Cin(adder_full_4_2_cout), .Cout(Cout), .S(S[7:4]));
  Adder_full_4 adder_full_4_2 (.A(A[3:0]), .B(B[3:0]), .Cin(Cin), .Cout(adder_full_4_2_cout), .S(S[3:0]));
endmodule

module Adder_full_16 (
  input  [15:0] B,
  input  [15:0] A,
  input  Cin,
  output Cout,
  output [15:0] S
);

  wire adder_full_8_2_cout;

  Adder_full_8 adder_full_8_1 (.A(A[15:8]), .B(B[15:8]), .Cin(adder_full_8_2_cout), .Cout(Cout), .S(S[15:8]));
  Adder_full_8 adder_full_8_2 (.A(A[7:0]), .B(B[7:0]), .Cin(Cin), .Cout(adder_full_8_2_cout), .S(S[7:0]));
endmodule

module Adder_full_32 (
  input  [31:0] B,
  input  [31:0] A,
  input  Cin,
  output Cout,
  output [31:0] S
);

  wire adder_full_16_2_cout;

  Adder_full_16 adder_full_16_1 (.B(A[31:16]), .A(B[31:16]), .Cin(adder_full_16_2_cout), .Cout(Cout), .S(S[31:16]));
  Adder_full_16 adder_full_16_2 (.B(A[15:0]), .A(B[15:0]), .Cin(Cin), .Cout(adder_full_16_2_cout), .S(S[15:0]));
endmodule

module Adder_full_17 (
  input  [16:0] a,
  input  [16:0] b,
  input  Cin,
  output Cout,
  output [16:0] sum
);

  wire adder_full_16_1_cout;

  Adder_full adder_full_1 (.cin(adder_full_16_1_cout), .a(a[16]), .b(b[16]), .sum(sum[16]), .cout(Cout));
  Adder_full_16 adder_full_16_1 (.B(a[15:0]), .A(b[15:0]), .Cin(Cin), .Cout(adder_full_16_1_cout), .S(sum[15:0]));

  // Other names for the same wires on the sheet: a_15[15:0] = a[15:0]; a_16 = a[16]; b_15[15:0] = b[15:0];
  //   b_16 = b[16]
endmodule

module Sub_half (
  input  a,
  input  b,
  output D,
  output Bout
);

  xor xor_1 (D, a, b);
  and and_1 (Bout, ~a, b);  // AND_Gate
endmodule

module Sub_full (
  input  a,
  input  Bin,
  input  b,
  output D,
  output Bout
);

  wire sub_half_1_bout, sub_half_1_d, sub_half_2_bout;

  Sub_half sub_half_1 (.a(a), .b(b), .D(sub_half_1_d), .Bout(sub_half_1_bout));
  or or_1 (Bout, sub_half_1_bout, sub_half_2_bout);
  Sub_half sub_half_2 (.a(sub_half_1_d), .b(Bin), .D(D), .Bout(sub_half_2_bout));
endmodule

module Original_Adder_full_4 (
  input  Symbol_A,
  input  A3,
  input  A2,
  input  A1,
  input  A0,
  input  Symbol_B,
  input  B3,
  input  B2,
  input  B1,
  input  B0,
  output Symbol,
  output Y3,
  output Y2,
  output Y1,
  output Y0
);

  wire AEB, AGB, ALB, and_1_out, and_2_out, and_3_out, nosame_Sym_S0, nosame_Sym_S1, nosame_Sym_S2,
       nosame_Sym_S3, same_Sym, same_Sym_S0, same_Sym_S1, same_Sym_S2, same_Sym_S3, xor_1_out;
  wire [3:0] selector_4_2_1_1_y, selector_4_2_1_2_y;

  xor xor_1 (xor_1_out, Symbol_A, Symbol_B);
  Comparator_4 comparator_4_1 (
    .A3(A3), .A2(A2), .A1(A1), .A0(A0), .B3(B3), .B2(B2), .B1(B1), .B0(B0), .E_IN(1'b1), .G(AGB), .E(AEB),
    .L(ALB));  // open: G_IN, L_IN
  not not_1 (same_Sym, xor_1_out);
  Selector_4_2_1 selector_4_2_1_1 (.S0(AGB), .A1({A3, A2, A1, A0}), .A0({B3, B2, B1, B0}), .Y(selector_4_2_1_1_y));
  Selector_4_2_1 selector_4_2_1_2 (.S0(ALB), .A1({A3, A2, A1, A0}), .A0({B3, B2, B1, B0}), .Y(selector_4_2_1_2_y));
  Sub_full_4 sub_full_4_1 (
    .A3(selector_4_2_1_1_y[3]), .A2(selector_4_2_1_1_y[2]), .A1(selector_4_2_1_1_y[1]),
    .A0(selector_4_2_1_1_y[0]), .B3(selector_4_2_1_2_y[3]), .B2(selector_4_2_1_2_y[2]),
    .B1(selector_4_2_1_2_y[1]), .B0(selector_4_2_1_2_y[0]), .D3(nosame_Sym_S3), .D2(nosame_Sym_S2),
    .D1(nosame_Sym_S1), .D0(nosame_Sym_S0));  // open: Bin, Bout
  // Adder_full_4 adder_full_4_1: pin names not known; wires that end beside it: A3, B3, A2, B2, same_Sym_S3, same_Sym_S2, same_Sym_S1
  and and_1 (and_1_out, same_Sym, Symbol_A);
  and and_2 (and_2_out, ~same_Sym, Symbol_A, AGB);  // AND_Gate
  and and_3 (and_3_out, ~same_Sym, Symbol_B, ALB);  // AND_Gate
  or or_1 (Symbol, and_1_out, and_2_out, and_3_out);
  Selector_4_2_1 selector_4_2_1_3 (
    .S0(same_Sym), .A1({same_Sym_S3, same_Sym_S2, same_Sym_S1, same_Sym_S0}),
    .A0({nosame_Sym_S3, nosame_Sym_S2, nosame_Sym_S1, nosame_Sym_S0}), .Y({Y3, Y2, Y1, Y0}));
endmodule

module Sub_full_4 (
  input  A3,
  input  A2,
  input  A1,
  input  A0,
  input  B3,
  input  B2,
  input  B1,
  input  B0,
  input  Bin,
  output Bout,
  output D3,
  output D2,
  output D1,
  output D0
);

  wire sub_full_2_bout, sub_full_3_bout, sub_full_4_bout;

  Sub_full sub_full_1 (.a(A3), .Bin(sub_full_2_bout), .b(B3), .D(D3), .Bout(Bout));
  Sub_full sub_full_2 (.a(A2), .Bin(sub_full_3_bout), .b(B2), .D(D2), .Bout(sub_full_2_bout));
  Sub_full sub_full_3 (.a(A1), .Bin(sub_full_4_bout), .b(B1), .D(D1), .Bout(sub_full_3_bout));
  Sub_full sub_full_4 (.a(A0), .Bin(Bin), .b(B0), .D(D0), .Bout(sub_full_4_bout));
endmodule

module One_s_complement_Adder_full_4 (
  input  Symbol_A,
  input  A3,
  input  A2,
  input  A1,
  input  A0,
  input  Symbol_B,
  input  B3,
  input  B2,
  input  B1,
  input  B0,
  output Symbol,
  output Y3,
  output Y2,
  output Y1,
  output Y0
);

  wire A0_t, A1_t, A2_t, A3_t, B0_t, B1_t, B2_t, B3_t, original_adder_full_4_1_y0,
       original_adder_full_4_1_y1, original_adder_full_4_1_y2, original_adder_full_4_1_y3;

  not not_1 (A3_t, A3);
  not not_2 (A2_t, A2);
  not not_3 (A1_t, A1);
  not not_4 (A0_t, A0);
  not not_5 (B3_t, B3);
  not not_6 (B2_t, B2);
  not not_7 (B1_t, B1);
  not not_8 (B0_t, B0);
  Original_Adder_full_4 original_adder_full_4_1 (
    .Symbol_A(Symbol_A), .A3(A3_t), .A2(A2_t), .A1(A1_t), .A0(A0_t), .Symbol_B(Symbol_B), .B3(B3_t),
    .B2(B2_t), .B1(B1_t), .B0(B0_t), .Symbol(Symbol), .Y3(original_adder_full_4_1_y3),
    .Y2(original_adder_full_4_1_y2), .Y1(original_adder_full_4_1_y1), .Y0(original_adder_full_4_1_y0));
  not not_9 (Y3, original_adder_full_4_1_y3);
  not not_10 (Y2, original_adder_full_4_1_y2);
  not not_11 (Y1, original_adder_full_4_1_y1);
  not not_12 (Y0, original_adder_full_4_1_y0);
endmodule

module Complement_Adder_16 (
  input  symbol_a,
  input  [15:0] a,
  input  symbol_b,
  input  [15:0] b,
  output [15:0] sum,
  output symbol_sum,
  output Overflow
);

  wire not_3_out, or_1_out, xor_1_out, xor_2_out, zero;
  wire [15:0] acom, acom_0, adder_full_16_3_s, bcom, bcom_0, com_sum_16, not_1_out, not_2_out, not_4_out,
       selector_16_2_1_3_y;

  assign not_1_out = ~a;  // NOT_Gate not_1, 16 bits wide
  assign not_2_out = ~b;  // NOT_Gate not_2, 16 bits wide
  Selector_16_2_1 selector_16_2_1_1 (.S0(symbol_a), .A0(a), .A1(acom_0), .Y(acom));
  Adder_full_16 adder_full_16_1 (.B(not_1_out), .A(16'h1), .S(acom_0));  // open: Cin, Cout
  Adder_full_16 adder_full_16_2 (.B(not_2_out), .A(16'h1), .S(bcom_0));  // open: Cin, Cout
  Selector_16_2_1 selector_16_2_1_2 (.S0(symbol_b), .A0(b), .A1(bcom_0), .Y(bcom));
  xor xor_1 (xor_1_out, symbol_a, symbol_b);
  not not_3 (not_3_out, xor_1_out);
  xor xor_2 (xor_2_out, symbol_a, symbol_sum);
  and and_1 (Overflow, not_3_out, xor_2_out);
  // Probe on {symbol_a, acom}
  // Probe on {symbol_b, bcom}
  Adder_full_17 adder_full_17_1 (
    .a({symbol_a, acom}), .b({symbol_b, bcom}), .sum({symbol_sum, com_sum_16}));  // open: Cin, Cout
  // Probe on {symbol_sum, com_sum_16}
  assign not_4_out = ~com_sum_16;  // NOT_Gate not_4, 16 bits wide
  Adder_full_16 adder_full_16_3 (.B(not_4_out), .A(16'h1), .S(adder_full_16_3_s));  // open: Cin, Cout
  Selector_16_2_1 selector_16_2_1_3 (.S0(symbol_sum), .A0(com_sum_16), .A1(adder_full_16_3_s), .Y(selector_16_2_1_3_y));
  or or_1 (or_1_out, b[0], b[1], b[2], b[3], b[4], b[5], b[6], b[7], b[9], b[10], b[11], b[12], b[13], b[14], b[15], b[8]);
  not not_5 (zero, or_1_out);
  Selector_16_2_1 selector_16_2_1_4 (.S0(zero), .A0(selector_16_2_1_3_y), .A1(a), .Y(sum));

  // Other names for the same wires on the sheet: acom_1[15:0] = acom; acom[16] = symbol_a; bcom_1[15:0] = bcom;
  //   bcom[16] = symbol_b; com_sum_17[16:0] = {symbol_sum, com_sum_16}
endmodule

module SR_AND_latch (
  input  S,
  input  R,
  input  rst_n,
  output Q,
  output Q0
);

  wire and_1_out, and_2_out, and_3_out, or_1_out;

  or or_1 (or_1_out, S, ~rst_n);  // OR_Gate
  and and_1 (and_1_out, R, rst_n);
  and and_2 (and_2_out, or_1_out, Q0);
  not not_1 (Q, and_2_out);
  and and_3 (and_3_out, and_1_out, Q);
  not not_2 (Q0, and_3_out);
endmodule

module SR_OR_latch (
  input  S,
  input  R,
  output Q,
  output Q0
);

  wire or_1_out, or_2_out;

  or or_1 (or_1_out, S, Q0);
  or or_2 (or_2_out, R, Q);
  not not_1 (Q, or_1_out);
  not not_2 (Q0, or_2_out);
endmodule

module D_latch_Synchronization (
  input  rst_n,
  input  D,
  input  WE,
  output Q,
  output Q0
);

  wire and_1_out, and_2_out, and_3_out, not_1_out, not_2_out, not_3_out;

  and and_1 (and_1_out, rst_n, D);
  not not_1 (not_1_out, and_1_out);
  and and_2 (and_2_out, and_1_out, WE);
  not not_2 (not_2_out, and_2_out);
  and and_3 (and_3_out, WE, not_1_out);
  not not_3 (not_3_out, and_3_out);
  SR_AND_latch sr_and_latch_1 (.S(not_2_out), .R(not_3_out), .rst_n(not_3_out), .Q(Q), .Q0(Q0));
endmodule

module D_latch_Asynchronous (
  input  D,
  input  rst_n,
  input  WE,
  output Q,
  output Q0
);

  wire and_1_out, and_2_out, not_1_out, not_2_out, not_3_out;

  not not_1 (not_1_out, D);
  and and_1 (and_1_out, D, WE);
  not not_2 (not_2_out, and_1_out);
  and and_2 (and_2_out, WE, not_1_out);
  not not_3 (not_3_out, and_2_out);
  SR_AND_latch sr_and_latch_1 (.S(not_2_out), .R(not_3_out), .rst_n(rst_n), .Q(Q), .Q0(Q0));
endmodule

module Edge_D_flip_flop (
  input  rst_n,
  input  EN,
  input  D,
  input  clk,
  output Q,
  output Q0
);

  wire d_latch_asynchronous_1_q, not_1_out, selector_1_2_1_1_y;

  Selector_1_2_1 selector_1_2_1_1 (.S(EN), .A1(D), .A0(Q), .Y(selector_1_2_1_1_y));
  not not_1 (not_1_out, clk);
  D_latch_Asynchronous d_latch_asynchronous_1 (
    .D(selector_1_2_1_1_y), .rst_n(rst_n), .WE(clk), .Q(d_latch_asynchronous_1_q));  // open: Q0
  D_latch_Asynchronous d_latch_asynchronous_2 (
    .D(d_latch_asynchronous_1_q), .rst_n(rst_n), .WE(not_1_out), .Q(Q), .Q0(Q0));
endmodule

module Register_4 (
  input  [3:0] D,
  input  clk,
  input  EN,
  input  rst_n,
  output [3:0] Q
);

  Edge_D_flip_flop edge_d_flip_flop_1 (.rst_n(rst_n), .EN(EN), .D(D[3]), .clk(clk), .Q(Q[3]));  // open: Q0
  Edge_D_flip_flop edge_d_flip_flop_2 (.rst_n(rst_n), .EN(EN), .D(D[2]), .clk(clk), .Q(Q[2]));  // open: Q0
  Edge_D_flip_flop edge_d_flip_flop_3 (.rst_n(rst_n), .EN(EN), .D(D[1]), .clk(clk), .Q(Q[1]));  // open: Q0
  Edge_D_flip_flop edge_d_flip_flop_4 (.rst_n(rst_n), .EN(EN), .D(D[0]), .clk(clk), .Q(Q[0]));  // open: Q0

  // Other names for the same wires on the sheet: D_0 = D[0]; D_1 = D[1]; D_2 = D[2]; D_3 = D[3]; Q_0 = Q[0];
  //   Q_1 = Q[1]; Q_2 = Q[2]; Q_3 = Q[3]
endmodule

module Register_8 (
  input  [7:0] D,
  input  clk,
  input  EN,
  input  rst_n,
  output [7:0] Q
);

  Register_4 register_4_1 (.D(D[7:4]), .clk(clk), .EN(EN), .rst_n(rst_n), .Q(Q[7:4]));
  Register_4 register_4_2 (.D(D[3:0]), .clk(clk), .EN(EN), .rst_n(rst_n), .Q(Q[3:0]));

  // Other names for the same wires on the sheet: D_0[3:0] = D[3:0]; D_1[3:0] = D[7:4]; Q_0[3:0] = Q[3:0];
  //   Q_1[3:0] = Q[7:4]
endmodule

module Register_16 (
  input  [15:0] D,
  input  clk,
  input  EN,
  input  rst_n,
  output [15:0] Q
);

  Register_4 register_4_1 (.D(D[15:12]), .clk(clk), .EN(EN), .rst_n(rst_n), .Q(Q[15:12]));
  Register_4 register_4_2 (.D(D[11:8]), .clk(clk), .EN(EN), .rst_n(rst_n), .Q(Q[11:8]));
  Register_4 register_4_3 (.D(D[7:4]), .clk(clk), .EN(EN), .rst_n(rst_n), .Q(Q[7:4]));
  Register_4 register_4_4 (.D(D[3:0]), .clk(clk), .EN(EN), .rst_n(rst_n), .Q(Q[3:0]));

  // Other names for the same wires on the sheet: D_0[3:0] = D[3:0]; D_1[3:0] = D[7:4]; D_2[3:0] = D[11:8];
  //   D_3[3:0] = D[15:12]; Q_0[3:0] = Q[3:0]; Q_1[3:0] = Q[7:4]; Q_2[3:0] = Q[11:8]; Q_3[3:0] = Q[15:12]
endmodule

module Register_32 (
  input  [31:0] D,
  input  clk,
  input  EN,
  input  rst_n,
  output [31:0] Q
);

  Register_16 register_16_1 (.D(D[31:16]), .clk(clk), .EN(EN), .rst_n(rst_n), .Q(Q[31:16]));
  Register_16 register_16_2 (.D(D[15:0]), .clk(clk), .EN(EN), .rst_n(rst_n), .Q(Q[15:0]));

  // Other names for the same wires on the sheet: D_0[15:0] = D[15:0]; D_1[15:0] = D[31:16]; Q_0[15:0] = Q[15:0];
  //   Q_1[15:0] = Q[31:16]
endmodule

module Counter_16 (
  input  set_value_n,
  input  [15:0] Initial_value,
  input  clk,
  input  EN,
  input  rst_n,
  output [15:0] Q,
  output over_flow
);

  wire [15:0] selector_16_2_1_1_y, sum;

  Selector_16_2_1 selector_16_2_1_1 (.S0(set_value_n), .A0(Initial_value), .A1(sum), .Y(selector_16_2_1_1_y));
  Register_16 register_16_1 (.D(selector_16_2_1_1_y), .clk(clk), .EN(EN), .rst_n(rst_n), .Q(Q));
  Adder_full_16 adder_full_16_1 (.B(Q), .A({16{1'b0}}), .Cin(1'b1), .Cout(over_flow), .S(sum));
endmodule

module Counter_32 (
  input  set_value_n,
  input  clk,
  input  EN,
  input  rst_n,
  input  [31:0] Initial_value,
  output [31:0] Q,
  output over_flow
);

  wire [31:0] selector_32_2_1_1_y, sum;

  Selector_32_2_1 selector_32_2_1_1 (.S0(set_value_n), .A1(sum), .A0(Initial_value), .Y(selector_32_2_1_1_y));
  Register_32 register_32_1 (.D(selector_32_2_1_1_y), .clk(clk), .EN(EN), .rst_n(rst_n), .Q(Q));
  Adder_full_32 adder_full_32_1 (.B(Q), .A({32{1'b0}}), .Cin(1'b1), .Cout(over_flow), .S(sum));
endmodule

module Sum_of_a_sequence (
  input  set_value_n,
  input  [15:0] Initial_value,
  input  clk,
  input  EN,
  input  rst_n,
  output over_flow,
  output [15:0] Q
);

  wire [15:0] counter_16_1_q, register_16_1_q;

  Counter_16 counter_16_1 (
    .set_value_n(set_value_n), .Initial_value(Initial_value), .clk(clk), .EN(EN), .rst_n(rst_n),
    .Q(counter_16_1_q));  // open: over_flow
  // Probe on counter_16_1_q
  // Probe on register_16_1_q
  Register_16 register_16_1 (.D(Q), .clk(clk), .EN(EN), .rst_n(rst_n), .Q(register_16_1_q));
  Adder_full_16 adder_full_16_1 (.B(counter_16_1_q), .A(register_16_1_q), .Cout(over_flow), .S(Q));  // open: Cin
  // Probe on Q
endmodule

module The_clock (
  input  EN,
  input  clk,
  input  rst_n,
  output [15:0] h,
  output [15:0] seconds,
  output [15:0] min
);

  wire nand_1_out, nand_2_out, nand_3_out;

  Counter_16 counter_16_1 (
    .set_value_n(nand_1_out), .Initial_value({16{1'b0}}), .clk(nand_2_out), .EN(EN), .rst_n(rst_n), .Q(h));  // open: over_flow
  nand nand_1 (nand_1_out, h[0], h[1], h[2], h[3], ~h[4], h[5]);  // NAND_Gate
  Counter_16 counter_16_2 (
    .set_value_n(nand_2_out), .Initial_value({16{1'b0}}), .clk(nand_3_out), .EN(EN), .rst_n(rst_n), .Q(min));  // open: over_flow
  nand nand_2 (nand_2_out, ~min[0], ~min[1], min[2], min[3], min[4], min[5]);  // NAND_Gate
  Counter_16 counter_16_3 (
    .set_value_n(nand_3_out), .Initial_value({16{1'b0}}), .clk(clk), .EN(EN), .rst_n(rst_n), .Q(seconds));  // open: over_flow
  nand nand_3 (nand_3_out, ~seconds[0], ~seconds[1], seconds[2], seconds[3], seconds[4], seconds[5]);  // NAND_Gate
endmodule

module The_clock_Temple (
  input  in_1,
  input  in_2
);

  wire a_0, a_1, a_2, a_3, a_4, a_5, b_0, b_1, b_2, b_3, b_4, b_5, c_0, c_1, c_2, c_3, c_4, c_5, clock_1_out,
       d_0, d_1, d_2, d_3, d_4, d_5, e_0, e_1, e_2, e_3, e_4, e_5, f_0, f_1, f_2, f_3, f_4, f_5, g_0, g_1,
       g_2, g_3, g_4, g_5;
  wire [15:0] h, min, seconds;

  Clock clock_1 (.out(clock_1_out));
  Clock clock_2 ();  // open: out
  The_clock the_clock_1 (.EN(in_1), .clk(clock_1_out), .rst_n(in_2), .h(h), .seconds(seconds), .min(min));
  // Probe on seconds
  _7_Segment_Display u_7_segment_display_1 (.g(g_4), .f(f_4), .a(a_4), .b(b_4), .e(e_4), .d(d_4), .c(c_4));  // open: dp
  _7_Segment_Display u_7_segment_display_2 (.g(g_5), .f(f_5), .a(a_5), .b(b_5), .e(e_5), .d(d_5), .c(c_5));  // open: dp
  _7_Segment_Display u_7_segment_display_3 (.g(g_3), .f(f_3), .a(a_3), .b(b_3), .e(e_3), .d(d_3), .c(c_3));  // open: dp
  _7_Segment_Display u_7_segment_display_4 (.g(g_2), .f(f_2), .a(a_2), .b(b_2), .e(e_2), .d(d_2), .c(c_2));  // open: dp
  _7_Segment_Display u_7_segment_display_5 (.g(g_1), .f(f_1), .a(a_1), .b(b_1), .e(e_1), .d(d_1), .c(c_1));  // open: dp
  _7_Segment_Display u_7_segment_display_6 (.g(g_0), .f(f_0), .a(a_0), .b(b_0), .e(e_0), .d(d_0), .c(c_0));  // open: dp
  Decoder_min_seconds_SEG decoder_min_seconds_seg_1 (
    .min_seconds(seconds), .EN(in_1),
    .a0_g0_a1_g1({g_1, f_1, e_1, d_1, c_1, b_1, a_1, g_0, f_0, e_0, d_0, c_0, b_0, a_0}));
  Decoder_min_seconds_SEG decoder_min_seconds_seg_2 (
    .min_seconds(min), .EN(in_1),
    .a0_g0_a1_g1({g_3, f_3, e_3, d_3, c_3, b_3, a_3, g_2, f_2, e_2, d_2, c_2, b_2, a_2}));
  Decoder_min_seconds_SEG decoder_min_seconds_seg_3 (
    .min_seconds(h), .EN(in_1),
    .a0_g0_a1_g1({g_5, f_5, e_5, d_5, c_5, b_5, a_5, g_4, f_4, e_4, d_4, c_4, b_4, a_4}));

  // Other names for the same wires on the sheet: EN = in_1
endmodule

module sCPU (
  input  clk,
  input  rst_n,
  input  EN,
  input  [7:0] inst,
  output [3:0] out_pc,
  output Perid_en,
  output [3:0] Perid_sn,
  output [7:0] cpu_outdb
);

  wire adder_full_4_1_cout, EX_pc_wen, exu_1_reg_wen;
  wire [1:0] exu_1_rd_reg, exu_1_reg_rs1, exu_1_reg_rs2, idu_1_opcode, idu_1_rd, idu_1_rs1, idu_1_rs2,
       selector_2_2_1_1_y;
  wire [3:0] adder_full_4_1_s, EX_npc, idu_1_addr, idu_1_imm, selector_4_2_1_1_y;
  wire [7:0] exu_1_reg_wdata, my_ram_1_q_r0, my_ram_1_q_r1;

  IDU idu_1 (
    .inst(inst), .opcode(idu_1_opcode), .rd(idu_1_rd), .rs1(idu_1_rs1), .rs2(idu_1_rs2), .addr(idu_1_addr),
    .imm(idu_1_imm));
  Adder_full_4 adder_full_4_1 (.A(out_pc), .B(4'b0001), .Cin(1'b0), .Cout(adder_full_4_1_cout), .S(adder_full_4_1_s));
  EXU exu_1 (
    .opcode(idu_1_opcode), .rd(idu_1_rd), .rs1(idu_1_rs1), .rs2(idu_1_rs2), .addr(idu_1_addr),
    .imm(idu_1_imm), .reg_rdata1(my_ram_1_q_r0), .reg_rdata2(my_ram_1_q_r1), .reg_rs1(exu_1_reg_rs1),
    .reg_rs2(exu_1_reg_rs2), .reg_wdata(exu_1_reg_wdata), .reg_wen(exu_1_reg_wen), .rd_reg(exu_1_rd_reg),
    .EX_npc(EX_npc), .EX_pc_wen(EX_pc_wen), .Perid_en(Perid_en), .Perid_sn(Perid_sn), .out_data(cpu_outdb));  // open: PC
  // Probe on EX_npc
  Selector_4_2_1 selector_4_2_1_1 (.S0(EX_pc_wen), .A1(EX_npc), .A0(adder_full_4_1_s), .Y(selector_4_2_1_1_y));
  // Probe on exu_1_reg_wdata
  Selector_2_2_1 selector_2_2_1_1 (.S0(exu_1_reg_wen), .A1(exu_1_rd_reg), .A0(exu_1_reg_rs1), .Y(selector_2_2_1_1_y));
  // Probe on out_pc
  Register_4 PC (.D(selector_4_2_1_1_y), .clk(clk), .EN(EN), .rst_n(rst_n), .Q(out_pc));
  my_RAM my_ram_1 (
    .clk(clk), .rst_n(rst_n), .D(exu_1_reg_wdata), .R0_W_ADDR(selector_2_2_1_1_y), .W_EN(exu_1_reg_wen),
    .R1_ADDR(exu_1_reg_rs2), .Q_R0(my_ram_1_q_r0), .Q_R1(my_ram_1_q_r1));

  // Other names for the same wires on the sheet: PC[3:0] = out_pc
endmodule

module my_ROM (
  input  [3:0] ADDR,
  output [7:0] inst
);

  // Probe on 8'hdf
  // Probe on 8'hd1
  // Probe on 8'h17
  // Probe on 8'h29
  // Probe on 8'hb1
  // Probe on 8'ha0
  // Probe on 8'h90
  // Probe on 8'h8a
  // Probe on 8'hdf
  // Probe on 8'hd1
  // Probe on 8'h17
  // Probe on 8'h29
  // Probe on 8'hb2
  // Probe on 8'ha0
  // Probe on 8'h91
  // Probe on 8'h8b
  // Probe on 8'he3
  // Probe on 8'hd1
  // Probe on 8'h17
  // Probe on 8'h29
  // Probe on 8'h42
  // Probe on 8'hb2
  // Probe on 8'ha0
  // Probe on 8'h91
  // Probe on 8'h8b
  Selector_8_16_1 selector_8_16_1_1 (
    .A7(8'hdf), .A6(8'hd1), .A5(8'h17), .A4(8'h29), .A3(8'hb1), .A2(8'ha0), .A1(8'h90), .A0(8'h8a));  // open: S, A15, A14, A13, A12, A11, A10, A9, A8, Y
  Selector_8_16_1 selector_8_16_1_2 (
    .A7(8'hdf), .A6(8'hd1), .A5(8'h17), .A4(8'h29), .A3(8'hb2), .A2(8'ha0), .A1(8'h91), .A0(8'h8b));  // open: S, A15, A14, A13, A12, A11, A10, A9, A8, Y
  Selector_8_16_1 selector_8_16_1_3 (
    .S(ADDR), .A8(8'he3), .A7(8'hd1), .A6(8'h17), .A5(8'h29), .A4(8'h42), .A3(8'hb2), .A2(8'ha0), .A1(8'h91),
    .A0(8'h8b), .Y(inst));  // open: A15, A14, A13, A12, A11, A10, A9

  // Notes on the sheet:
  //   自然数求和
  //   奇数求和
  //   out_rs
  //   第四条和第五条要交换一下从0开始加，这样奇数求和直接改步长就行不然就会变成2468求和
endmodule

module my_RAM (
  input  clk,
  input  rst_n,
  input  [7:0] D,
  input  [1:0] R0_W_ADDR,
  input  W_EN,
  input  [1:0] R1_ADDR,
  output [7:0] Q_R0,
  output [7:0] Q_R1
);

  wire decoder_2_4_1_y0, decoder_2_4_1_y1, decoder_2_4_1_y2, decoder_2_4_1_y3;
  wire [7:0] register_8_1_q, register_8_2_q, register_8_3_q, register_8_4_q;

  Decoder_2_4 decoder_2_4_1 (
    .en(W_EN), .A(R0_W_ADDR[1]), .B(R0_W_ADDR[0]), .Y0(decoder_2_4_1_y0), .Y1(decoder_2_4_1_y1),
    .Y2(decoder_2_4_1_y2), .Y3(decoder_2_4_1_y3));
  // Probe on R0_W_ADDR
  // Probe on register_8_1_q
  // Probe on register_8_2_q
  Register_8 register_8_1 (.D(D), .clk(clk), .EN(decoder_2_4_1_y3), .rst_n(rst_n), .Q(register_8_1_q));
  Register_8 register_8_2 (.D(D), .clk(clk), .EN(decoder_2_4_1_y2), .rst_n(rst_n), .Q(register_8_2_q));
  // Probe on register_8_3_q
  Register_8 register_8_3 (.D(D), .clk(clk), .EN(decoder_2_4_1_y1), .rst_n(rst_n), .Q(register_8_3_q));
  Register_8 register_8_4 (.D(D), .clk(clk), .EN(decoder_2_4_1_y0), .rst_n(rst_n), .Q(register_8_4_q));
  // Probe on register_8_4_q
  Selector_8_4_1 selector_8_4_1_1 (
    .S(R0_W_ADDR), .A3(register_8_1_q), .A2(register_8_2_q), .A1(register_8_3_q), .A0(register_8_4_q),
    .Y(Q_R0));
  Selector_8_4_1 selector_8_4_1_2 (
    .S(R1_ADDR), .A3(register_8_1_q), .A2(register_8_2_q), .A1(register_8_3_q), .A0(register_8_4_q), .Y(Q_R1));
endmodule

module IDU (
  input  [7:0] inst,
  output [1:0] opcode,
  output [1:0] rd,
  output [1:0] rs1,
  output [1:0] rs2,
  output [3:0] addr,
  output [3:0] imm
);


  assign addr = inst[5:2];
  assign imm = inst[3:0];
  assign opcode = inst[7:6];
  assign rd = inst[5:4];
  assign rs1 = inst[3:2];
  assign rs2 = inst[1:0];
endmodule

module EXU (
  input  [1:0] opcode,
  input  [1:0] rd,
  input  [1:0] rs1,
  input  [1:0] rs2,
  input  [3:0] addr,
  input  [3:0] imm,
  input  [7:0] reg_rdata1,
  input  [7:0] reg_rdata2,
  input  [3:0] PC,
  output [1:0] reg_rs1,
  output [1:0] reg_rs2,
  output [7:0] reg_wdata,
  output reg_wen,
  output [1:0] rd_reg,
  output [3:0] EX_npc,
  output EX_pc_wen,
  output Perid_en,
  output [3:0] Perid_sn,
  output [7:0] out_data
);

  wire add, bner0, li, out_rs, r0_b_rs2, selector_1_2_1_1_y, selector_1_2_1_2_y;
  wire [7:0] selector_8_2_1_1_y, sum_registers;

  Comparator_2 comparator_2_1 (.A(opcode), .B(2'b01), .G_IN(1'b0), .E_IN(1'b1), .L_IN(1'b0), .E(out_rs));  // open: G, L
  Comparator_2 comparator_2_2 (.A(opcode), .B(2'b00), .G_IN(1'b0), .E_IN(1'b1), .L_IN(1'b0), .E(add));  // open: G, L
  Comparator_2 comparator_2_3 (.A(opcode), .B(2'b10), .G_IN(1'b0), .E_IN(1'b1), .L_IN(1'b0), .E(li));  // open: G, L
  Comparator_2 comparator_2_4 (.A(opcode), .B(2'b11), .G_IN(1'b0), .E_IN(1'b1), .L_IN(1'b0), .E(bner0));  // open: G, L
  // Probe on reg_rdata1
  // Probe on reg_rdata2
  Adder_full_8 adder_full_8_1 (.A(reg_rdata1), .B(reg_rdata2), .Cin(1'b0), .S(sum_registers));  // open: Cout
  // Probe on reg_rdata1
  // Probe on reg_rdata2
  Selector_2_2_1 selector_2_2_1_1 (.S0(bner0), .A1(2'b00), .A0(rs1), .Y(reg_rs1));
  Selector_4_2_1 selector_4_2_1_1 (.S0(bner0), .A1(addr), .A0(4'b0000), .Y(EX_npc));
  // Probe on sum_registers
  Comparator_8 comparator_8_1 (
    .a(reg_rdata1), .b(reg_rdata2), .G_IN(1'b0), .E_IN(1'b1), .L_IN(1'b0), .E(r0_b_rs2));  // open: G, L
  // Probe on reg_rs1
  // Probe on rs2
  // Probe on r0_b_rs2
  Selector_1_2_1 selector_1_2_1_1 (.S(li), .A1(1'b1), .A0(1'b0), .Y(selector_1_2_1_1_y));
  Selector_1_2_1 selector_1_2_1_2 (.S(r0_b_rs2), .A1(1'b0), .A0(1'b1), .Y(selector_1_2_1_2_y));
  Selector_8_2_1 selector_8_2_1_1 (.S0(li), .A1({4'b0000, imm}), .A0({8{1'b0}}), .Y(selector_8_2_1_1_y));
  Selector_1_2_1 selector_1_2_1_3 (.S(add), .A1(1'b1), .A0(selector_1_2_1_1_y), .Y(reg_wen));
  Selector_1_2_1 selector_1_2_1_4 (.S(out_rs), .A1(1'b1), .A0(1'b0), .Y(Perid_en));
  Selector_1_2_1 selector_1_2_1_5 (.S(bner0), .A1(selector_1_2_1_2_y), .A0(1'b0), .Y(EX_pc_wen));
  Selector_8_2_1 selector_8_2_1_2 (.S0(add), .A1(sum_registers), .A0(selector_8_2_1_1_y), .Y(reg_wdata));
  // Probe on reg_wdata

  assign out_data = reg_rdata2;
  assign Perid_sn = addr;
  assign rd_reg = rd;
  assign reg_rs2 = rs2;
endmodule

module computer (
  input  clk,
  input  rst_n,
  input  EN
);

  wire a_0, a_1, and_1_out, b_0, b_1, c_0, c_1, d_0, d_1, decoder_4_16_new_1_y0, e_0, e_1, f_0, f_1, g_0,
       g_1, scpu_1_perid_en;
  wire [3:0] scpu_1_out_pc, scpu_1_perid_sn;
  wire [7:0] cpu_outdb, my_rom_1_inst;

  _7_Segment_Display u_7_segment_display_1 (.g(g_1), .f(f_1), .a(a_1), .b(b_1), .e(e_1), .d(d_1), .c(c_1));  // open: dp
  _7_Segment_Display u_7_segment_display_2 (.g(g_0), .f(f_0), .a(a_0), .b(b_0), .e(e_0), .d(d_0), .c(c_0));  // open: dp
  // Probe on scpu_1_out_pc
  // Probe on my_rom_1_inst
  my_ROM my_rom_1 (.ADDR(scpu_1_out_pc), .inst(my_rom_1_inst));
  sCPU scpu_1 (
    .clk(clk), .rst_n(rst_n), .EN(EN), .inst(my_rom_1_inst), .out_pc(scpu_1_out_pc),
    .Perid_en(scpu_1_perid_en), .Perid_sn(scpu_1_perid_sn), .cpu_outdb(cpu_outdb));
  Decoder_4_16_new decoder_4_16_new_1 (
    .A(scpu_1_perid_sn), .en(EN), .Y0(decoder_4_16_new_1_y0));  // open: Y1, Y2, Y3, Y4, Y5, Y6, Y7, Y8, Y9, Y10, Y11, Y12, Y13, Y14, Y15
  and and_1 (and_1_out, scpu_1_perid_en, decoder_4_16_new_1_y0);
  Decoder_min_seconds_SEG decoder_min_seconds_seg_1 (
    .min_seconds({{8{1'b0}}, cpu_outdb}), .EN(and_1_out),
    .a0_g0_a1_g1({g_1, f_1, e_1, d_1, c_1, b_1, a_1, g_0, f_0, e_0, d_0, c_0, b_0, a_0}));
endmodule

module risc_v (
  input  clk,
  input  rst_n,
  input  EN,
  input  [31:0] inst,
  input  [31:0] ram_r_data,
  output [31:0] pc,
  output [31:0] ram_addr,
  output ram_wen,
  output [31:0] ram_w_data,
  output [3:0] ram_boe
);

  wire EX_pc_wen, not_1_out, risc_v_exu_1_reg_wen;
  wire [2:0] risc_v_idu_1_funct3;
  wire [4:0] risc_v_exu_1_reg_raddr_0, risc_v_exu_1_reg_raddr_1, risc_v_exu_1_reg_w_addr, risc_v_idu_1_rd,
       risc_v_idu_1_rs1, risc_v_idu_1_rs2;
  wire [6:0] risc_v_idu_1_funct7, risc_v_idu_1_opcode;
  wire [31:0] adder_1_out, EX_npc, multiplexer_1_out, reg_rdata0, reg_rdata1, risc_v_exu_1_reg_wdata,
       risc_v_idu_1_b_imm, risc_v_idu_1_i_imm, risc_v_idu_1_j_imm, risc_v_idu_1_s_imm, risc_v_idu_1_u_imm;

  Clock clock_1 ();  // open: out
  // Probe on inst
  Adder #(.width(32)) adder_1 (.a(pc), .b(32'h4), .out(adder_1_out), .cin(1'b0));  // open: cout
  risc_v_IDU risc_v_idu_1 (
    .inst(inst), .opcode(risc_v_idu_1_opcode), .rd(risc_v_idu_1_rd), .funct3(risc_v_idu_1_funct3),
    .rs1(risc_v_idu_1_rs1), .rs2(risc_v_idu_1_rs2), .funct7(risc_v_idu_1_funct7), .I_imm(risc_v_idu_1_i_imm),
    .S_imm(risc_v_idu_1_s_imm), .B_imm(risc_v_idu_1_b_imm), .U_imm(risc_v_idu_1_u_imm),
    .J_imm(risc_v_idu_1_j_imm));
  // Probe on risc_v_idu_1_rd
  Multiplexer #(.width(32)) multiplexer_1 (.in0(adder_1_out), .in1(EX_npc), .out(multiplexer_1_out), .sel(EX_pc_wen));
  risc_v_EXU risc_v_exu_1 (
    .opcode(risc_v_idu_1_opcode), .rd(risc_v_idu_1_rd), .funct3(risc_v_idu_1_funct3), .rs1(risc_v_idu_1_rs1),
    .rs2(risc_v_idu_1_rs2), .funct7(risc_v_idu_1_funct7), .I_imm(risc_v_idu_1_i_imm),
    .S_imm(risc_v_idu_1_s_imm), .B_imm(risc_v_idu_1_b_imm), .U_imm(risc_v_idu_1_u_imm),
    .J_imm(risc_v_idu_1_j_imm), .reg_rdata0(reg_rdata0), .reg_rdata1(reg_rdata1), .pc(pc),
    .ram_rdata(ram_r_data), .reg_raddr_0(risc_v_exu_1_reg_raddr_0), .reg_raddr_1(risc_v_exu_1_reg_raddr_1),
    .reg_w_addr(risc_v_exu_1_reg_w_addr), .reg_wdata(risc_v_exu_1_reg_wdata), .reg_wen(risc_v_exu_1_reg_wen),
    .EX_npc(EX_npc), .EX_pc_wen(EX_pc_wen), .ram_addr(ram_addr), .ram_wen(ram_wen), .ram_wdata(ram_w_data),
    .ram_boe(ram_boe));
  Register #(.width(32)) register_1 (.D(multiplexer_1_out), .en(EN), .clk(clk), .Q(pc), .clr(not_1_out));
  // Probe on pc
  not not_1 (not_1_out, rst_n);
  rv32_reg rv32_reg_1 (
    .clk(clk), .rst_n(rst_n), .D(risc_v_exu_1_reg_wdata), .W_EN(risc_v_exu_1_reg_wen),
    .R0_W_ADDR(risc_v_exu_1_reg_w_addr), .R_ADDR_0(risc_v_exu_1_reg_raddr_0),
    .R_ADDR_1(risc_v_exu_1_reg_raddr_1), .DQ_0(reg_rdata0), .DQ_1(reg_rdata1));
endmodule

module rv32_reg (
  input  clk,
  input  rst_n,
  input  [31:0] D,
  input  W_EN,
  input  [4:0] R0_W_ADDR,
  input  [4:0] R_ADDR_0,
  input  [4:0] R_ADDR_1,
  output [31:0] DQ_0,
  output [31:0] DQ_1
);

  wire rst_n_t;
  wire [4:0] not_2_out, not_3_out;
  wire [31:0] decoder_5_32_1_y, register_1_q, register_2_q, register_3_q, register_4_q, register_5_q,
       register_6_q, register_7_q, register_8_q, register_9_q, register_10_q, register_11_q, register_12_q,
       register_13_q, register_14_q, register_15_q, register_16_q, register_17_q, register_18_q,
       register_19_q, register_20_q, register_21_q, register_22_q, register_23_q, register_24_q,
       register_25_q, register_26_q, register_27_q, register_28_q, register_29_q, register_30_q,
       register_31_q;

  not not_1 (rst_n_t, rst_n);
  Decoder_5_32 decoder_5_32_1 (.A(R0_W_ADDR), .en(W_EN), .Y(decoder_5_32_1_y));
  Register #(.width(32)) register_1 (.D(D), .en(decoder_5_32_1_y[31]), .clk(clk), .Q(register_1_q), .clr(rst_n_t));
  Register #(.width(32)) register_2 (.D(D), .en(decoder_5_32_1_y[30]), .clk(clk), .Q(register_2_q), .clr(rst_n_t));
  Register #(.width(32)) register_3 (.D(D), .en(decoder_5_32_1_y[29]), .clk(clk), .Q(register_3_q), .clr(rst_n_t));
  Register #(.width(32)) register_4 (.D(D), .en(decoder_5_32_1_y[28]), .clk(clk), .Q(register_4_q), .clr(rst_n_t));
  Register #(.width(32)) register_5 (.D(D), .en(decoder_5_32_1_y[27]), .clk(clk), .Q(register_5_q), .clr(rst_n_t));
  Register #(.width(32)) register_6 (.D(D), .en(decoder_5_32_1_y[26]), .clk(clk), .Q(register_6_q), .clr(rst_n_t));
  Register #(.width(32)) register_7 (.D(D), .en(decoder_5_32_1_y[25]), .clk(clk), .Q(register_7_q), .clr(rst_n_t));
  Register #(.width(32)) register_8 (.D(D), .en(decoder_5_32_1_y[24]), .clk(clk), .Q(register_8_q), .clr(rst_n_t));
  Register #(.width(32)) register_9 (.D(D), .en(decoder_5_32_1_y[23]), .clk(clk), .Q(register_9_q), .clr(rst_n_t));
  Register #(.width(32)) register_10 (.D(D), .en(decoder_5_32_1_y[22]), .clk(clk), .Q(register_10_q), .clr(rst_n_t));
  Register #(.width(32)) register_11 (.D(D), .en(decoder_5_32_1_y[21]), .clk(clk), .Q(register_11_q), .clr(rst_n_t));
  Register #(.width(32)) register_12 (.D(D), .en(decoder_5_32_1_y[20]), .clk(clk), .Q(register_12_q), .clr(rst_n_t));
  Register #(.width(32)) register_13 (.D(D), .en(decoder_5_32_1_y[19]), .clk(clk), .Q(register_13_q), .clr(rst_n_t));
  Register #(.width(32)) register_14 (.D(D), .en(decoder_5_32_1_y[18]), .clk(clk), .Q(register_14_q), .clr(rst_n_t));
  Register #(.width(32)) register_15 (.D(D), .en(decoder_5_32_1_y[17]), .clk(clk), .Q(register_15_q), .clr(rst_n_t));
  Register #(.width(32)) register_16 (.D(D), .en(decoder_5_32_1_y[16]), .clk(clk), .Q(register_16_q), .clr(rst_n_t));
  Register #(.width(32)) register_17 (.D(D), .en(decoder_5_32_1_y[15]), .clk(clk), .Q(register_17_q), .clr(rst_n_t));
  Register #(.width(32)) register_18 (.D(D), .en(decoder_5_32_1_y[14]), .clk(clk), .Q(register_18_q), .clr(rst_n_t));
  Register #(.width(32)) register_19 (.D(D), .en(decoder_5_32_1_y[13]), .clk(clk), .Q(register_19_q), .clr(rst_n_t));
  Register #(.width(32)) register_20 (.D(D), .en(decoder_5_32_1_y[12]), .clk(clk), .Q(register_20_q), .clr(rst_n_t));
  Register #(.width(32)) register_21 (.D(D), .en(decoder_5_32_1_y[11]), .clk(clk), .Q(register_21_q), .clr(rst_n_t));
  Register #(.width(32)) register_22 (.D(D), .en(decoder_5_32_1_y[10]), .clk(clk), .Q(register_22_q), .clr(rst_n_t));
  Register #(.width(32)) register_23 (.D(D), .en(decoder_5_32_1_y[9]), .clk(clk), .Q(register_23_q), .clr(rst_n_t));
  Register #(.width(32)) register_24 (.D(D), .en(decoder_5_32_1_y[8]), .clk(clk), .Q(register_24_q), .clr(rst_n_t));
  Register #(.width(32)) register_25 (.D(D), .en(decoder_5_32_1_y[7]), .clk(clk), .Q(register_25_q), .clr(rst_n_t));
  Register #(.width(32)) register_26 (.D(D), .en(decoder_5_32_1_y[6]), .clk(clk), .Q(register_26_q), .clr(rst_n_t));
  Register #(.width(32)) register_27 (.D(D), .en(decoder_5_32_1_y[5]), .clk(clk), .Q(register_27_q), .clr(rst_n_t));
  Register #(.width(32)) register_28 (.D(D), .en(decoder_5_32_1_y[4]), .clk(clk), .Q(register_28_q), .clr(rst_n_t));
  Register #(.width(32)) register_29 (.D(D), .en(decoder_5_32_1_y[3]), .clk(clk), .Q(register_29_q), .clr(rst_n_t));
  Register #(.width(32)) register_30 (.D(D), .en(decoder_5_32_1_y[2]), .clk(clk), .Q(register_30_q), .clr(rst_n_t));
  Register #(.width(32)) register_31 (.D(D), .en(decoder_5_32_1_y[1]), .clk(clk), .Q(register_31_q), .clr(rst_n_t));
  // Probe on register_1_q
  // Probe on register_2_q
  // Probe on register_3_q
  // Probe on register_4_q
  // Probe on register_5_q
  // Probe on register_6_q
  // Probe on register_7_q
  // Probe on register_8_q
  // Probe on register_9_q
  // Probe on register_10_q
  // Probe on register_11_q
  // Probe on register_12_q
  // Probe on register_13_q
  // Probe on register_14_q
  // Probe on register_15_q
  // Probe on register_16_q
  // Probe on register_17_q
  // Probe on register_18_q
  // Probe on register_19_q
  // Probe on register_20_q
  // Probe on register_21_q
  // Probe on register_22_q
  // Probe on register_23_q
  // Probe on register_24_q
  // Probe on register_25_q
  // Probe on register_26_q
  // Probe on register_27_q
  // Probe on register_28_q
  // Probe on register_29_q
  // Probe on register_30_q
  // Probe on register_31_q
  Multiplexer #(.select(5), .width(32)) multiplexer_1 (
    .in0(register_1_q), .in1(register_2_q), .in2(register_3_q), .in3(register_4_q), .in4(register_5_q),
    .in5(register_6_q), .in6(register_7_q), .in7(register_8_q), .in8(register_9_q), .in9(register_10_q),
    .in10(register_11_q), .in11(register_12_q), .in12(register_13_q), .in13(register_14_q),
    .in14(register_15_q), .in15(register_16_q), .in16(register_17_q), .in17(register_18_q),
    .in18(register_19_q), .in19(register_20_q), .in20(register_21_q), .in21(register_22_q),
    .in22(register_23_q), .in23(register_24_q), .in24(register_25_q), .in25(register_26_q),
    .in26(register_27_q), .in27(register_28_q), .in28(register_29_q), .in29(register_30_q),
    .in30(register_31_q), .in31({32{1'b0}}), .out(DQ_0), .sel(not_2_out));
  Multiplexer #(.select(5), .width(32)) multiplexer_2 (
    .in0(register_1_q), .in1(register_2_q), .in2(register_3_q), .in3(register_4_q), .in4(register_5_q),
    .in5(register_6_q), .in6(register_7_q), .in7(register_8_q), .in8(register_9_q), .in9(register_10_q),
    .in10(register_11_q), .in11(register_12_q), .in12(register_13_q), .in13(register_14_q),
    .in14(register_15_q), .in15(register_16_q), .in16(register_17_q), .in17(register_18_q),
    .in18(register_19_q), .in19(register_20_q), .in20(register_21_q), .in21(register_22_q),
    .in22(register_23_q), .in23(register_24_q), .in24(register_25_q), .in25(register_26_q),
    .in26(register_27_q), .in27(register_28_q), .in28(register_29_q), .in29(register_30_q),
    .in30(register_31_q), .in31({32{1'b0}}), .out(DQ_1), .sel(not_3_out));
  assign not_2_out = ~R_ADDR_0;  // NOT_Gate not_2, 5 bits wide
  // Probe on not_3_out
  assign not_3_out = ~R_ADDR_1;  // NOT_Gate not_3, 5 bits wide
  // Probe on R_ADDR_1
endmodule

module risc_v_IDU (
  input  [31:0] inst,
  output [6:0] opcode,
  output [4:0] rd,
  output [2:0] funct3,
  output [4:0] rs1,
  output [4:0] rs2,
  output [6:0] funct7,
  output [31:0] I_imm,
  output [31:0] S_imm,
  output [31:0] B_imm,
  output [31:0] U_imm,
  output [31:0] J_imm
);

  // Probe on inst[11:7]
  assign I_imm[31:11] = {{20{inst[31]}}, inst[31]};  // Bit_Extender bit_extender_1
  assign S_imm[31:11] = {{20{inst[31]}}, inst[31]};  // Bit_Extender bit_extender_2
  assign B_imm[31:12] = {{19{inst[31]}}, inst[31]};  // Bit_Extender bit_extender_3
  assign J_imm[31:20] = {{11{inst[31]}}, inst[31]};  // Bit_Extender bit_extender_4

  assign B_imm[11:0] = {inst[7], inst[30:25], inst[11:8], 1'b0};
  assign funct3 = inst[14:12];
  assign funct7 = inst[31:25];
  assign I_imm[10:0] = inst[30:20];
  assign J_imm[19:0] = {inst[19:12], inst[20], inst[30:21], 1'b0};
  assign opcode = inst[6:0];
  assign rd = inst[11:7];
  assign rs1 = inst[19:15];
  assign rs2 = inst[24:20];
  assign S_imm[10:0] = {inst[30:25], inst[11:7]};
  assign U_imm = {inst[31:12], {12{1'b0}}};
endmodule

module risc_v_EXU (
  input  [6:0] opcode,
  input  [4:0] rd,
  input  [2:0] funct3,
  input  [4:0] rs1,
  input  [4:0] rs2,
  input  [6:0] funct7,
  input  [31:0] I_imm,
  input  [31:0] S_imm,
  input  [31:0] B_imm,
  input  [31:0] U_imm,
  input  [31:0] J_imm,
  input  [31:0] reg_rdata0,
  input  [31:0] reg_rdata1,
  input  [31:0] pc,
  input  [31:0] ram_rdata,
  output [4:0] reg_raddr_0,
  output [4:0] reg_raddr_1,
  output [4:0] reg_w_addr,
  output [31:0] reg_wdata,
  output reg_wen,
  output [31:0] EX_npc,
  output EX_pc_wen,
  output [31:0] ram_addr,
  output ram_wen,
  output [31:0] ram_wdata,
  output [3:0] ram_boe
);

  wire add, addi, comparator_3_1_e, comparator_3_2_e, comparator_3_3_e, comparator_3_4_e, comparator_3_5_e,
       comparator_3_6_e, comparator_3_7_e, comparator_7_1_e, comparator_7_2_e, comparator_7_3_e,
       comparator_7_5_e, comparator_7_6_e, comparator_7_7_e, comparator_7_8_e, jalr, lbu, lui, lw,
       multiplexer_20_out, or_1_out, or_2_out, or_3_out, or_4_out, or_5_out, or_6_out, or_7_out, sb, sw;
  wire [3:0] decoder_1_out0;
  wire [7:0] multiplexer_18_out;
  wire [31:0] alu_sum, alu_sum1, and_8_out, bit_extender_1_out, multiplexer_2_out, multiplexer_3_out,
       multiplexer_5_out, multiplexer_6_out, multiplexer_7_out, multiplexer_8_out, multiplexer_9_out,
       multiplexer_10_out, multiplexer_12_out, multiplexer_13_out, multiplexer_15_out, multiplexer_16_out,
       multiplexer_17_out, multiplexer_23_out, not_1_out;

  // Probe on reg_rdata0
  Comparator_3 comparator_3_1 (
    .A(funct3), .B(3'b000), .G_IN(1'b0), .E_IN(1'b1), .L_IN(1'b0), .E(comparator_3_1_e));  // open: G, L
  Comparator_7 comparator_7_1 (
    .A(opcode), .B(7'b0010011), .G_IN(1'b0), .E_IN(1'b1), .L_IN(1'b0), .E(comparator_7_1_e));  // open: G, L
  Comparator_3 comparator_3_2 (
    .A(funct3), .B(3'b000), .G_IN(1'b0), .E_IN(1'b1), .L_IN(1'b0), .E(comparator_3_2_e));  // open: G, L
  Comparator_7 comparator_7_2 (
    .A(opcode), .B(7'b1100111), .G_IN(1'b0), .E_IN(1'b1), .L_IN(1'b0), .E(comparator_7_2_e));  // open: G, L
  Comparator_3 comparator_3_3 (
    .A(funct3), .B(3'b000), .G_IN(1'b0), .E_IN(1'b1), .L_IN(1'b0), .E(comparator_3_3_e));  // open: G, L
  Comparator_7 comparator_7_3 (
    .A(opcode), .B(7'b0110011), .G_IN(1'b0), .E_IN(1'b1), .L_IN(1'b0), .E(comparator_7_3_e));  // open: G, L
  Comparator_7 comparator_7_4 (
    .A(opcode), .B(7'b0110111), .G_IN(1'b0), .E_IN(1'b1), .L_IN(1'b0), .E(lui));  // open: G, L
  Comparator_3 comparator_3_4 (
    .A(funct3), .B(3'b010), .G_IN(1'b0), .E_IN(1'b1), .L_IN(1'b0), .E(comparator_3_4_e));  // open: G, L
  Comparator_7 comparator_7_5 (
    .A(opcode), .B(7'b0000011), .G_IN(1'b0), .E_IN(1'b1), .L_IN(1'b0), .E(comparator_7_5_e));  // open: G, L
  Comparator_3 comparator_3_5 (
    .A(funct3), .B(3'b010), .G_IN(1'b0), .E_IN(1'b1), .L_IN(1'b0), .E(comparator_3_5_e));  // open: G, L
  Comparator_7 comparator_7_6 (
    .A(opcode), .B(7'b0100011), .G_IN(1'b0), .E_IN(1'b1), .L_IN(1'b0), .E(comparator_7_6_e));  // open: G, L
  Comparator_3 comparator_3_6 (
    .A(funct3), .B(3'b100), .G_IN(1'b0), .E_IN(1'b1), .L_IN(1'b0), .E(comparator_3_6_e));  // open: G, L
  Comparator_7 comparator_7_7 (
    .A(opcode), .B(7'b0000011), .G_IN(1'b0), .E_IN(1'b1), .L_IN(1'b0), .E(comparator_7_7_e));  // open: G, L
  Comparator_3 comparator_3_7 (
    .A(funct3), .B(3'b000), .G_IN(1'b0), .E_IN(1'b1), .L_IN(1'b0), .E(comparator_3_7_e));  // open: G, L
  Comparator_7 comparator_7_8 (
    .A(opcode), .B(7'b0100011), .G_IN(1'b0), .E_IN(1'b1), .L_IN(1'b0), .E(comparator_7_8_e));  // open: G, L
  and and_1 (addi, comparator_3_1_e, comparator_7_1_e);
  and and_2 (jalr, comparator_3_2_e, comparator_7_2_e);
  and and_3 (add, comparator_3_3_e, comparator_7_3_e);
  and and_4 (lw, comparator_3_4_e, comparator_7_5_e);
  and and_5 (sw, comparator_3_5_e, comparator_7_6_e);
  and and_6 (lbu, comparator_3_6_e, comparator_7_7_e);
  and and_7 (sb, comparator_3_7_e, comparator_7_8_e);
  // Probe on or_1_out
  or or_1 (or_1_out, jalr, add, lui, addi, lbu, lw, sw, sb);
  Multiplexer multiplexer_1 (.in0(1'b0), .in1(1'b1), .out(EX_pc_wen), .sel(jalr));
  Multiplexer #(.width(32)) multiplexer_2 (.in0({32{1'b0}}), .in1(reg_rdata0), .out(multiplexer_2_out), .sel(add));
  Multiplexer #(.width(32)) multiplexer_3 (.in0({32{1'b0}}), .in1(reg_rdata1), .out(multiplexer_3_out), .sel(add));
  // Probe on reg_rdata0
  Multiplexer #(.width(32)) multiplexer_4 (.in0({32{1'b0}}), .in1(and_8_out), .out(EX_npc), .sel(jalr));
  assign and_8_out = not_1_out & alu_sum1;  // AND_Gate and_8, 32 bits wide
  assign not_1_out = ~32'h1;  // NOT_Gate not_1, 32 bits wide
  or or_2 (or_2_out, sw, sb);
  Multiplexer #(.width(32)) multiplexer_5 (.in0({32{1'b0}}), .in1(reg_rdata0), .out(multiplexer_5_out), .sel(or_2_out));
  Multiplexer #(.width(32)) multiplexer_6 (.in0({32{1'b0}}), .in1(S_imm), .out(multiplexer_6_out), .sel(or_2_out));
  Multiplexer #(.width(32)) multiplexer_7 (.in0(multiplexer_2_out), .in1(pc), .out(multiplexer_7_out), .sel(jalr));
  Multiplexer #(.width(32)) multiplexer_8 (.in0(multiplexer_3_out), .in1(32'h4), .out(multiplexer_8_out), .sel(jalr));
  or or_3 (or_3_out, jalr, lbu, lw);
  Multiplexer #(.width(32)) multiplexer_9 (
    .in0(multiplexer_5_out), .in1(reg_rdata0), .out(multiplexer_9_out), .sel(or_3_out));
  Multiplexer #(.width(32)) multiplexer_10 (
    .in0(multiplexer_6_out), .in1(I_imm), .out(multiplexer_10_out), .sel(or_3_out));
  Multiplexer multiplexer_11 (.in0(1'b0), .in1(1'b1), .out(reg_wen), .sel(or_4_out));
  or or_4 (or_4_out, lui, lw, add, addi, jalr, lbu);
  Multiplexer #(.width(32)) multiplexer_12 (
    .in0(multiplexer_7_out), .in1(reg_rdata0), .out(multiplexer_12_out), .sel(addi));
  Multiplexer #(.width(32)) multiplexer_13 (.in0(multiplexer_8_out), .in1(I_imm), .out(multiplexer_13_out), .sel(addi));
  Adder #(.width(32)) adder_1 (
    .a(multiplexer_9_out), .b(multiplexer_10_out), .out(alu_sum1), .cin(1'b0));  // open: cout
  Adder #(.width(32)) adder_2 (
    .a(multiplexer_12_out), .b(multiplexer_13_out), .out(alu_sum), .cin(1'b0));  // open: cout
  Multiplexer #(.width(32)) multiplexer_14 (.in0(multiplexer_15_out), .in1(alu_sum), .out(reg_wdata), .sel(or_5_out));
  Multiplexer #(.width(32)) multiplexer_15 (.in0(multiplexer_16_out), .in1(U_imm), .out(multiplexer_15_out), .sel(lui));
  Multiplexer #(.width(32)) multiplexer_16 (
    .in0(multiplexer_17_out), .in1(ram_rdata), .out(multiplexer_16_out), .sel(lw));
  Multiplexer #(.width(32)) multiplexer_17 (
    .in0({32{1'b0}}), .in1(bit_extender_1_out), .out(multiplexer_17_out), .sel(lbu));
  Multiplexer #(.select(2), .width(8)) multiplexer_18 (
    .in0(ram_rdata[7:0]), .in1(ram_rdata[15:8]), .in2(ram_rdata[23:16]), .in3(ram_rdata[31:24]),
    .out(multiplexer_18_out), .sel(ram_addr[1:0]));
  // Probe on bit_extender_1_out
  assign bit_extender_1_out = {{24{1'b0}}, multiplexer_18_out};  // Bit_Extender bit_extender_1
  or or_5 (or_5_out, addi, add, jalr);
  Multiplexer multiplexer_19 (.in0(multiplexer_20_out), .in1(1'b0), .out(ram_wen), .sel(lw));
  Multiplexer multiplexer_20 (.in0(1'b0), .in1(1'b1), .out(multiplexer_20_out), .sel(or_6_out));
  or or_6 (or_6_out, sw, sb);
  Multiplexer #(.width(32)) multiplexer_21 (.in0({32{1'b0}}), .in1(alu_sum1), .out(ram_addr), .sel(or_7_out));
  or or_7 (or_7_out, lw, lbu, sw, sb);
  // Probe on alu_sum1
  Multiplexer #(.width(32)) multiplexer_22 (.in0(multiplexer_23_out), .in1(reg_rdata1), .out(ram_wdata), .sel(sw));
  // Probe on reg_rdata1
  Multiplexer #(.width(32)) multiplexer_23 (
    .in0({32{1'b0}}), .in1({reg_rdata1[7:0], reg_rdata1[7:0], reg_rdata1[7:0], reg_rdata1[7:0]}),
    .out(multiplexer_23_out), .sel(sb));
  Multiplexer #(.width(4)) multiplexer_24 (.in0(4'b1111), .in1(decoder_1_out0), .out(ram_boe), .sel(sb));
  Decoder #(.select(2)) decoder_1 (
    .out0(decoder_1_out0[0]), .out1(decoder_1_out0[1]), .out2(decoder_1_out0[2]), .out3(decoder_1_out0[3]),
    .sel(ram_addr[1:0]), .en(1'b1));

  assign reg_raddr_0 = rs1;
  assign reg_raddr_1 = rs2;
  assign reg_w_addr = rd;

  // Notes on the sheet:
  //   addi
  //   jalr
  //   add
  //   lui
  //   lw
  //   sw
  //   lbu
  //   pc_wen
  //   EX_pc
  //   reg_wen
  //   alu
  //   reg_wdata
  //   ram_wen
  //   ram_addr
  //   ram_wdata
  //   ram_boe
endmodule

module risc_v_computer (
  input  clk,
  input  rst_n,
  input  EN
);

  wire and_1_out, clk_t, comparator_32_1_e, comparator_32_1_g, is_mem, is_vga, not_1_out, not_2_out,
       not_3_out, ram_wen;
  wire [3:0] ram_boe;
  wire [23:0] data;
  wire [31:0] inst, pc, ram_addr, ram_r_data;
  wire [31:24] ram_w_data;
  wire [63:0] counter_1_q;

  Clock clock_1 (.out(clk_t));
  and and_1 (and_1_out, is_mem, ram_wen);
  Counter #(.max('hffffffffffffffff), .width(64)) counter_1 (
    .clr(not_1_out), .load(1'b0), .up(1'b1), .count(EN), .clk(clk_t), .D({64{1'b0}}), .Q(counter_1_q));  // open: carry
  not not_1 (not_1_out, rst_n);
  // Probe on pc
  not not_2 (not_2_out, and_1_out);
  // Probe on {ram_w_data, data}
  RAM #(.addrWidth(20), .asyncread("true"), .byteenables("byteEnables"), .dataWidth(32), .\type ("nonvolatile")) ram_1 (
    .addr(ram_addr[21:2]), .we(and_1_out), .oe(not_2_out), .clk(clk_t), .din({ram_w_data, data}),
    .dout(ram_r_data), .be3(ram_boe[3]), .be2(ram_boe[2]), .be1(ram_boe[1]), .be0(ram_boe[0]));
  ROM #(.addrWidth(20), .dataWidth(32)) rom_1 (.addr(pc[21:2]), .data(inst));
  // Probe on counter_1_q
  // Probe on inst
  risc_v risc_v_1 (
    .clk(clk_t), .rst_n(rst_n), .EN(EN), .inst(inst), .ram_r_data(ram_r_data), .pc(pc), .ram_addr(ram_addr),
    .ram_wen(ram_wen), .ram_w_data({ram_w_data, data}), .ram_boe(ram_boe));
  not not_3 (not_3_out, rst_n);
  // RGB_Video #(.cursor("No Cursor"), .height(256), .width(256)) rgb_video_1: pin names not known; wires that end beside it: not_3_out, clk_t, is_vga, ram_addr[9:2], ram_addr[17:10], data
  Comparator_32 comparator_32_1 (
    .a(ram_addr), .b(32'h20000000), .G_IN(1'b0), .E_IN(1'b1), .L_IN(1'b0), .G(comparator_32_1_g),
    .E(comparator_32_1_e), .L(is_mem));
  or or_1 (is_vga, comparator_32_1_g, comparator_32_1_e);

  // Other names for the same wires on the sheet: x[7:0] = ram_addr[9:2]; y[7:0] = ram_addr[17:10];
  //   ram_w_data[23:0] = data

  // Notes on the sheet:
  //   contents of rom_1 (hex, n*v repeats v):
  //   1400513 10000e7 c000e7 c00067 a50513 8067
endmodule
